// Logisim project DD_ENCE2101_FinalProject_Dreiling.circ as structural Verilog: 34 circuits, main circuit Final_main
module Final_main (
  input  ped_active,
  input  en
);

  wire and_1_out, and_2_out, and_3_out, and_4_out, and_5_out, and_6_out, clk, full_fsm_1_g_off,
       full_fsm_1_ga, full_fsm_1_gb, full_fsm_1_r_on, full_fsm_1_ra, full_fsm_1_rb, full_fsm_1_y_off,
       full_fsm_1_ya, full_fsm_1_yb, G, GB, nState, or_1_out, or_2_out, or_9_out, pedestrian_button_1_p2,
       pedestrian_button_1_p6, R, RB, Y, YB;
  wire [3:0] downcount_10_0_1_count, DownCounter_v1_1_p3;
  wire [7:0] HEX0, HEX0C, HEX1, HEX1C;

  and and_1 (and_1_out, and_6_out, ped_active);
  and and_2 (and_2_out, ~DownCounter_v1_1_p3[0], ~DownCounter_v1_1_p3[1], ~DownCounter_v1_1_p3[2], ~DownCounter_v1_1_p3[3]);  // AND_Gate
  Clock u_clk (.out(clk));
  or or_1 (or_1_out, and_1_out, and_4_out);
  and and_3 (and_3_out, ~ped_active, en);  // AND_Gate
  and and_4 (and_4_out, en, and_2_out);
  or or_2 (or_2_out, nState, pedestrian_button_1_p2);
  FULL_FSM full_fsm_1 (
    .ped_active(ped_active), .en(and_3_out), .next_state(or_1_out), .G_off(full_fsm_1_g_off),
    .Y_off(full_fsm_1_y_off), .R_on(full_fsm_1_r_on), .GB(full_fsm_1_gb), .YB(full_fsm_1_yb),
    .RB(full_fsm_1_rb), .rst(nState), .GA(full_fsm_1_ga), .YA(full_fsm_1_ya), .RA(full_fsm_1_ra));
  // DownCounter_v1 DownCounter_v1_1: pin names not known; wires that end beside it: or_2_out, clk, DownCounter_v1_1_p3, DownCounter_v1_1_p3[3], DownCounter_v1_1_p3[2], DownCounter_v1_1_p3[1], DownCounter_v1_1_p3[0]
  // pedestrian_button pedestrian_button_1: pin names not known; wires that end beside it: DownCounter_v1_1_p3, pedestrian_button_1_p2
  or or_3 (GB, full_fsm_1_g_off, full_fsm_1_gb);
  or or_4 (YB, full_fsm_1_y_off, full_fsm_1_yb);
  or or_5 (RB, full_fsm_1_r_on, full_fsm_1_rb);
  or or_6 (G, full_fsm_1_ga, full_fsm_1_g_off);
  or or_7 (Y, full_fsm_1_ya, full_fsm_1_y_off);
  or or_8 (R, full_fsm_1_ra, full_fsm_1_r_on);
  // Bin2Hex_2 Bin2Hex_1: pin names not known; wires that end beside it: HEX1, HEX0
  // RGBLED RGBLED_1: pin names not known; wires that end beside it: R
  // RGBLED RGBLED_2: pin names not known; wires that end beside it: Y, Y
  // RGBLED RGBLED_3: pin names not known; wires that end beside it: G
  _7_Segment_Display #(.active("false")) u_7_segment_display_1 (
    .g(HEX1C[6]), .f(HEX1C[5]), .a(HEX1C[0]), .b(HEX1C[1]), .e(HEX1C[4]), .d(HEX1C[3]), .c(HEX1C[2]),
    .dp(HEX1C[7]));
  Clock clock_1 (.out(clk));
  and and_5 (and_5_out, nState, ped_active);
  _7_Segment_Display #(.active("false")) u_7_segment_display_2 (
    .g(HEX0C[6]), .f(HEX0C[5]), .a(HEX0C[0]), .b(HEX0C[1]), .e(HEX0C[4]), .d(HEX0C[3]), .c(HEX0C[2]),
    .dp(HEX0C[7]));
  or or_9 (or_9_out, and_5_out, pedestrian_button_1_p6);
  // RGBLED rgbled_1: pin names not known; wires that end beside it: RB
  // RGBLED rgbled_2: pin names not known; wires that end beside it: YB, YB
  // RGBLED rgbled_3: pin names not known; wires that end beside it: GB
  downcount_10_0 downcount_10_0_1 (.en(or_9_out), .clk(clk), .count(downcount_10_0_1_count));
  _7_Segment_Display #(.active("false")) L_7_Segment_Display_1 (
    .g(HEX1[6]), .f(HEX1[5]), .a(HEX1[0]), .b(HEX1[1]), .e(HEX1[4]), .d(HEX1[3]), .c(HEX1[2]), .dp(HEX1[7]));
  and and_6 (and_6_out, ~downcount_10_0_1_count[0], ~downcount_10_0_1_count[1], ~downcount_10_0_1_count[2], ~downcount_10_0_1_count[3]);  // AND_Gate
  // pedestrian_button pedestrian_button_1: pin names not known; wires that end beside it: downcount_10_0_1_count, downcount_10_0_1_count[0], downcount_10_0_1_count[1], downcount_10_0_1_count[2], downcount_10_0_1_count[3], pedestrian_button_1_p6, downcount_10_0_1_count[2], downcount_10_0_1_count[1], downcount_10_0_1_count[0]
  _7_Segment_Display #(.active("false")) L_7_Segment_Display_2 (
    .g(HEX0[6]), .f(HEX0[5]), .a(HEX0[0]), .b(HEX0[1]), .e(HEX0[4]), .d(HEX0[3]), .c(HEX0[2]), .dp(HEX0[7]));
  // Bin2Hex_2 bin2hex_2_1: pin names not known; wires that end beside it: downcount_10_0_1_count[3], HEX1C, HEX0C

  // Other names for the same wires on the sheet: PA = ped_active

  // Notes on the sheet:
  //   Traffic Light A
  //   Crosswalk timer
  //   Traffic Light B
  //   Counter_3sec
endmodule

module FSM_Light_B (
  input  en,
  input  next_state,
  output G,
  output Y,
  output R,
  output rst
);

  wire and_3_out, and_4_out;
  wire [1:0] multiplexer_1_out, register_1_q;

  Multiplexer #(.select(3), .width(2)) multiplexer_1 (
    .in0(2'b00), .in1(2'b01), .in2(2'b10), .in3(2'b11), .in4(2'b01), .in5(2'b10), .in6(2'b11), .in7(2'b00),
    .out(multiplexer_1_out), .sel({en, register_1_q}));
  // Probe on multiplexer_1_out
  Register #(.width(2)) register_1 (.D(multiplexer_1_out), .Q(register_1_q), .clk(next_state));  // open: en, clr
  // Probe on register_1_q
  and and_1 (G, ~register_1_q[0], ~register_1_q[1]);  // AND_Gate
  and and_2 (Y, register_1_q[0], ~register_1_q[1]);  // AND_Gate
  and and_3 (and_3_out, ~register_1_q[0], register_1_q[1]);  // AND_Gate
  and and_4 (and_4_out, register_1_q[0], register_1_q[1]);
  or or_1 (R, and_3_out, and_4_out);

  assign rst = next_state;

  // Notes on the sheet:
  //   Light B
endmodule

module FSM_Light_A (
  input  en,
  input  next_state,
  output G,
  output Y,
  output R,
  output rst
);

  wire and_3_out, and_4_out;
  wire [1:0] multiplexer_1_out, register_1_q;

  Multiplexer #(.select(3), .width(2)) multiplexer_1 (
    .in0(2'b00), .in1(2'b01), .in2(2'b10), .in3(2'b11), .in4(2'b01), .in5(2'b10), .in6(2'b11), .in7(2'b00),
    .out(multiplexer_1_out), .sel({en, register_1_q}));
  // Probe on multiplexer_1_out
  Register #(.width(2)) register_1 (.D(multiplexer_1_out), .Q(register_1_q), .clk(next_state));  // open: en, clr
  // Probe on register_1_q
  and and_1 (G, ~register_1_q[0], register_1_q[1]);  // AND_Gate
  and and_2 (Y, register_1_q[0], register_1_q[1]);
  and and_3 (and_3_out, ~register_1_q[0], ~register_1_q[1]);  // AND_Gate
  and and_4 (and_4_out, register_1_q[0], ~register_1_q[1]);  // AND_Gate
  or or_1 (R, and_3_out, and_4_out);

  assign rst = next_state;

  // Notes on the sheet:
  //   Light A
endmodule

module Testing (
  input  en
);

  wire and_1_out, and_2_out, clk, G, nState, or_1_out, pedestrian_button_1_p2, R, Y;
  wire [3:0] DownCounter_v1_1_p3;
  wire [7:0] HEX0, HEX1;

  and and_1 (and_1_out, ~DownCounter_v1_1_p3[0], ~DownCounter_v1_1_p3[1], ~DownCounter_v1_1_p3[2], ~DownCounter_v1_1_p3[3]);  // AND_Gate
  and and_2 (and_2_out, en, and_1_out);
  Clock u_clk (.out(clk));
  or or_1 (or_1_out, nState, pedestrian_button_1_p2);
  // RGBLED RGBLED_1: pin names not known; wires that end beside it: R
  // RGBLED RGBLED_2: pin names not known; wires that end beside it: Y, Y
  // RGBLED RGBLED_3: pin names not known; wires that end beside it: G
  FSM_Light_A fsm_light_a_1 (.en(en), .next_state(and_2_out), .G(G), .Y(Y), .R(R), .rst(nState));
  _7_Segment_Display #(.active("false")) L_7_Segment_Display_1 (
    .g(HEX1[6]), .f(HEX1[5]), .a(HEX1[0]), .b(HEX1[1]), .e(HEX1[4]), .d(HEX1[3]), .c(HEX1[2]), .dp(HEX1[7]));
  // DownCounter_v1 DownCounter_v1_1: pin names not known; wires that end beside it: or_1_out, clk, DownCounter_v1_1_p3, DownCounter_v1_1_p3[3], DownCounter_v1_1_p3[2], DownCounter_v1_1_p3[1], DownCounter_v1_1_p3[0]
  // pedestrian_button pedestrian_button_1: pin names not known; wires that end beside it: DownCounter_v1_1_p3, pedestrian_button_1_p2
  _7_Segment_Display #(.active("false")) L_7_Segment_Display_2 (
    .g(HEX0[6]), .f(HEX0[5]), .a(HEX0[0]), .b(HEX0[1]), .e(HEX0[4]), .d(HEX0[3]), .c(HEX0[2]), .dp(HEX0[7]));
  // Bin2Hex_2 Bin2Hex_1: pin names not known; wires that end beside it: HEX1, HEX0

  // Notes on the sheet:
  //   Traffic Light A
  //   Counter Display
endmodule

module testing2 (
  input  en,
  input  in_2
);

  wire and_1_out, and_2_out, and_3_out, and_4_out, clk, G, GB, nState, or_1_out, or_2_out,
       pedestrian_button_1_p2, pedestrian_button_1_p2_2, R, RB, Y, YB;
  wire [3:0] DownCounter_v1_1_p3, downcounter_v1_1_p3_2;
  wire [7:0] HEX0, HEX1;

  and and_1 (and_1_out, en, and_2_out);
  and and_2 (and_2_out, ~DownCounter_v1_1_p3[0], ~DownCounter_v1_1_p3[1], ~DownCounter_v1_1_p3[2], ~DownCounter_v1_1_p3[3]);  // AND_Gate
  Clock u_clk (.out(clk));
  and and_3 (and_3_out, ~downcounter_v1_1_p3_2[0], ~downcounter_v1_1_p3_2[1], ~downcounter_v1_1_p3_2[2], ~downcounter_v1_1_p3_2[3]);  // AND_Gate
  or or_1 (or_1_out, nState, pedestrian_button_1_p2);
  and and_4 (and_4_out, in_2, and_3_out);
  Clock clock_1 (.out(clk));
  or or_2 (or_2_out, nState, pedestrian_button_1_p2_2);
  FSM_Light_A fsm_light_a_1 (.en(en), .next_state(and_1_out), .G(G), .Y(Y), .R(R), .rst(nState));
  FSM_Light_B fsm_light_b_1 (.en(in_2), .next_state(and_4_out), .G(GB), .Y(YB), .R(RB), .rst(nState));
  // DownCounter_v1 DownCounter_v1_1: pin names not known; wires that end beside it: or_1_out, clk, DownCounter_v1_1_p3, DownCounter_v1_1_p3[3], DownCounter_v1_1_p3[2], DownCounter_v1_1_p3[1], DownCounter_v1_1_p3[0]
  // pedestrian_button pedestrian_button_1: pin names not known; wires that end beside it: DownCounter_v1_1_p3, pedestrian_button_1_p2
  _7_Segment_Display #(.active("false")) L_7_Segment_Display_1 (
    .g(HEX1[6]), .f(HEX1[5]), .a(HEX1[0]), .b(HEX1[1]), .e(HEX1[4]), .d(HEX1[3]), .c(HEX1[2]), .dp(HEX1[7]));
  // DownCounter_v1 downcounter_v1_1: pin names not known; wires that end beside it: or_2_out, clk, downcounter_v1_1_p3_2, downcounter_v1_1_p3_2[3], downcounter_v1_1_p3_2[2], downcounter_v1_1_p3_2[1], downcounter_v1_1_p3_2[0]
  // pedestrian_button pedestrian_button_1: pin names not known; wires that end beside it: downcounter_v1_1_p3_2, pedestrian_button_1_p2_2
  _7_Segment_Display #(.active("false")) L_7_Segment_Display_2 (
    .g(HEX0[6]), .f(HEX0[5]), .a(HEX0[0]), .b(HEX0[1]), .e(HEX0[4]), .d(HEX0[3]), .c(HEX0[2]), .dp(HEX0[7]));
  _7_Segment_Display #(.active("false")) u_7_segment_display_1 (
    .g(HEX1[6]), .f(HEX1[5]), .a(HEX1[0]), .b(HEX1[1]), .e(HEX1[4]), .d(HEX1[3]), .c(HEX1[2]), .dp(HEX1[7]));
  _7_Segment_Display #(.active("false")) u_7_segment_display_2 (
    .g(HEX0[6]), .f(HEX0[5]), .a(HEX0[0]), .b(HEX0[1]), .e(HEX0[4]), .d(HEX0[3]), .c(HEX0[2]), .dp(HEX0[7]));
  // Bin2Hex_2 Bin2Hex_1: pin names not known; wires that end beside it: HEX1, HEX0
  // Bin2Hex_2 bin2hex_2_1: pin names not known; wires that end beside it: HEX1, HEX0
  // RGBLED RGBLED_1: pin names not known; wires that end beside it: R
  // RGBLED RGBLED_2: pin names not known; wires that end beside it: Y, Y
  // RGBLED RGBLED_3: pin names not known; wires that end beside it: G
  // RGBLED rgbled_1: pin names not known; wires that end beside it: RB
  // RGBLED rgbled_2: pin names not known; wires that end beside it: YB, YB
  // RGBLED rgbled_3: pin names not known; wires that end beside it: GB

  // Notes on the sheet:
  //   Counter Display
  //   Counter Display
  //   Traffic Light A
  //   Traffic Light B
endmodule

module testing3_singleEnable (
  input  en
);

  wire and_1_out, and_2_out, and_3_out, and_4_out, clk, G, GB, nState, or_1_out, or_2_out,
       pedestrian_button_1_p2, pedestrian_button_1_p2_2, R, RB, Y, YB;
  wire [3:0] DownCounter_v1_1_p3, downcounter_v1_1_p3_2;
  wire [7:0] HEX0, HEX1;

  and and_1 (and_1_out, en, and_2_out);
  and and_2 (and_2_out, ~DownCounter_v1_1_p3[0], ~DownCounter_v1_1_p3[1], ~DownCounter_v1_1_p3[2], ~DownCounter_v1_1_p3[3]);  // AND_Gate
  Clock u_clk (.out(clk));
  and and_3 (and_3_out, ~downcounter_v1_1_p3_2[0], ~downcounter_v1_1_p3_2[1], ~downcounter_v1_1_p3_2[2], ~downcounter_v1_1_p3_2[3]);  // AND_Gate
  or or_1 (or_1_out, nState, pedestrian_button_1_p2_2);
  and and_4 (and_4_out, en, and_3_out);
  Clock clock_1 (.out(clk));
  or or_2 (or_2_out, nState, pedestrian_button_1_p2);
  FSM_Light_A fsm_light_a_1 (.en(en), .next_state(and_1_out), .G(G), .Y(Y), .R(R), .rst(nState));
  FSM_Light_B fsm_light_b_1 (.en(en), .next_state(and_4_out), .G(GB), .Y(YB), .R(RB), .rst(nState));
  // DownCounter_v1 DownCounter_v1_1: pin names not known; wires that end beside it: or_1_out, clk, DownCounter_v1_1_p3, DownCounter_v1_1_p3[3], DownCounter_v1_1_p3[2], DownCounter_v1_1_p3[1], DownCounter_v1_1_p3[0]
  // pedestrian_button pedestrian_button_1: pin names not known; wires that end beside it: DownCounter_v1_1_p3, pedestrian_button_1_p2_2
  _7_Segment_Display #(.active("false")) L_7_Segment_Display_1 (
    .g(HEX1[6]), .f(HEX1[5]), .a(HEX1[0]), .b(HEX1[1]), .e(HEX1[4]), .d(HEX1[3]), .c(HEX1[2]), .dp(HEX1[7]));
  // DownCounter_v1 downcounter_v1_1: pin names not known; wires that end beside it: or_2_out, clk, downcounter_v1_1_p3_2, downcounter_v1_1_p3_2[3], downcounter_v1_1_p3_2[2], downcounter_v1_1_p3_2[1], downcounter_v1_1_p3_2[0]
  // pedestrian_button pedestrian_button_1: pin names not known; wires that end beside it: downcounter_v1_1_p3_2, pedestrian_button_1_p2
  _7_Segment_Display #(.active("false")) L_7_Segment_Display_2 (
    .g(HEX0[6]), .f(HEX0[5]), .a(HEX0[0]), .b(HEX0[1]), .e(HEX0[4]), .d(HEX0[3]), .c(HEX0[2]), .dp(HEX0[7]));
  _7_Segment_Display #(.active("false")) u_7_segment_display_1 (
    .g(HEX1[6]), .f(HEX1[5]), .a(HEX1[0]), .b(HEX1[1]), .e(HEX1[4]), .d(HEX1[3]), .c(HEX1[2]), .dp(HEX1[7]));
  _7_Segment_Display #(.active("false")) u_7_segment_display_2 (
    .g(HEX0[6]), .f(HEX0[5]), .a(HEX0[0]), .b(HEX0[1]), .e(HEX0[4]), .d(HEX0[3]), .c(HEX0[2]), .dp(HEX0[7]));
  // Bin2Hex_2 Bin2Hex_1: pin names not known; wires that end beside it: HEX1, HEX0
  // Bin2Hex_2 bin2hex_2_1: pin names not known; wires that end beside it: HEX1, HEX0
  // RGBLED RGBLED_1: pin names not known; wires that end beside it: R
  // RGBLED RGBLED_2: pin names not known; wires that end beside it: Y, Y
  // RGBLED RGBLED_3: pin names not known; wires that end beside it: G
  // RGBLED rgbled_1: pin names not known; wires that end beside it: RB
  // RGBLED rgbled_2: pin names not known; wires that end beside it: YB, YB
  // RGBLED rgbled_3: pin names not known; wires that end beside it: GB

  // Notes on the sheet:
  //   Counter Display
  //   Counter Display
  //   Traffic Light A
  //   Traffic Light B
endmodule

module downcount_10_0 (
  input  en,
  input  clk,
  output [3:0] count
);

  wire and_1_out, and_2_out, and_3_out, and_4_out, t_ff_1_q, t_ff_2_q, t_ff_3_q;

  T_Flip_Flop t_ff_1 (.T(en), .clk(clk), .Q(t_ff_1_q), .Qn(count[0]), .preset(and_1_out));  // open: reset
  and and_1 (and_1_out, count[0], count[1], count[2], count[3]);
  and and_2 (and_2_out, en, t_ff_1_q);
  T_Flip_Flop t_ff_2 (.T(and_2_out), .clk(clk), .Q(t_ff_2_q), .Qn(count[1]));  // open: reset, preset
  and and_3 (and_3_out, and_2_out, t_ff_2_q);
  T_Flip_Flop t_ff_3 (.T(and_3_out), .clk(clk), .Q(t_ff_3_q), .Qn(count[2]), .preset(and_1_out));  // open: reset
  and and_4 (and_4_out, and_3_out, t_ff_3_q);
  T_Flip_Flop t_ff_4 (.T(and_4_out), .clk(clk), .Qn(count[3]));  // open: Q, reset, preset

  // Notes on the sheet:
  //   Synchronous Down Counter from 10 to 0 with reset
endmodule

module Crosswalk_layout (
  input  en
);

  wire clk, nState, or_1_out, pedestrian_button_1_p3;
  wire [3:0] downcount_10_0_1_count;
  wire [7:0] HEX0, HEX1;

  _7_Segment_Display #(.active("false")) L_7_Segment_Display_1 (
    .g(HEX1[6]), .f(HEX1[5]), .a(HEX1[0]), .b(HEX1[1]), .e(HEX1[4]), .d(HEX1[3]), .c(HEX1[2]), .dp(HEX1[7]));
  Clock u_clk (.out(clk));
  _7_Segment_Display #(.active("false")) L_7_Segment_Display_2 (
    .g(HEX0[6]), .f(HEX0[5]), .a(HEX0[0]), .b(HEX0[1]), .e(HEX0[4]), .d(HEX0[3]), .c(HEX0[2]), .dp(HEX0[7]));
  or or_1 (or_1_out, nState, pedestrian_button_1_p3);
  downcount_10_0 downcount_10_0_1 (.en(en), .clk(clk), .count(downcount_10_0_1_count));
  // pedestrian_button pedestrian_button_1: pin names not known; wires that end beside it: downcount_10_0_1_count, downcount_10_0_1_count, pedestrian_button_1_p3, downcount_10_0_1_count[2], downcount_10_0_1_count[1], downcount_10_0_1_count[0]
  // Bin2Hex_2 Bin2Hex_1: pin names not known; wires that end beside it: downcount_10_0_1_count[3], HEX1, HEX0

  // Notes on the sheet:
  //   Counter Display
endmodule

module testing_crosswalk_button (
);

  wire button_1_out, clk, or_1_out, pedestrian_button_1_p2;
  wire [3:0] downcount_10_0_1_count;
  wire [7:0] HEX0, HEX1;

  Button button_1 (.out(button_1_out));
  _7_Segment_Display #(.active("false")) L_7_Segment_Display_1 (
    .g(HEX1[6]), .f(HEX1[5]), .a(HEX1[0]), .b(HEX1[1]), .e(HEX1[4]), .d(HEX1[3]), .c(HEX1[2]), .dp(HEX1[7]));
  Clock u_clk (.out(clk));
  _7_Segment_Display #(.active("false")) L_7_Segment_Display_2 (
    .g(HEX0[6]), .f(HEX0[5]), .a(HEX0[0]), .b(HEX0[1]), .e(HEX0[4]), .d(HEX0[3]), .c(HEX0[2]), .dp(HEX0[7]));
  or or_1 (or_1_out, button_1_out, pedestrian_button_1_p2);
  downcount_10_0 downcount_10_0_1 (.en(or_1_out), .clk(clk), .count(downcount_10_0_1_count));
  // pedestrian_button pedestrian_button_1: pin names not known; wires that end beside it: downcount_10_0_1_count, pedestrian_button_1_p2, downcount_10_0_1_count, downcount_10_0_1_count[2], downcount_10_0_1_count[1], downcount_10_0_1_count[0]
  // Bin2Hex_2 Bin2Hex_1: pin names not known; wires that end beside it: downcount_10_0_1_count[3], HEX1, HEX0

  // Notes on the sheet:
  //   Counter Display
endmodule

module test_incorporate_button (
  input  en
);

  wire and_1_out, and_2_out, and_3_out, and_4_out, button_1_out, clk, G, GB, nState, or_1_out, or_2_out,
       or_3_out, pedestrian_button_1_p2, pedestrian_button_1_p2_2, pedestrian_button_2_p2, R, RB, Y, YB;
  wire [3:0] downcount_10_0_1_count, DownCounter_v1_1_p3, downcounter_v1_1_p3_2;
  wire [7:0] HEX0, HEX1, HEX02, HEX12;

  and and_1 (and_1_out, ~DownCounter_v1_1_p3[0], ~DownCounter_v1_1_p3[1], ~DownCounter_v1_1_p3[2], ~DownCounter_v1_1_p3[3]);  // AND_Gate
  and and_2 (and_2_out, en, and_1_out);
  Clock u_clk (.out(clk));
  and and_3 (and_3_out, ~downcounter_v1_1_p3_2[0], ~downcounter_v1_1_p3_2[1], ~downcounter_v1_1_p3_2[2], ~downcounter_v1_1_p3_2[3]);  // AND_Gate
  Clock clock_1 (.out(clk));
  or or_1 (or_1_out, nState, button_1_out, pedestrian_button_1_p2);
  and and_4 (and_4_out, en, and_3_out);
  or or_2 (or_2_out, nState, button_1_out, pedestrian_button_1_p2_2);
  FSM_Light_A fsm_light_a_1 (.en(en), .next_state(and_2_out), .G(G), .Y(Y), .R(R), .rst(nState));
  FSM_Light_B fsm_light_b_1 (.en(en), .next_state(and_4_out), .G(GB), .Y(YB), .R(RB), .rst(nState));
  _7_Segment_Display #(.active("false")) L_7_Segment_Display_1 (
    .g(HEX1[6]), .f(HEX1[5]), .a(HEX1[0]), .b(HEX1[1]), .e(HEX1[4]), .d(HEX1[3]), .c(HEX1[2]), .dp(HEX1[7]));
  // DownCounter_v1 DownCounter_v1_1: pin names not known; wires that end beside it: or_1_out, clk, DownCounter_v1_1_p3, DownCounter_v1_1_p3[3], DownCounter_v1_1_p3[2], DownCounter_v1_1_p3[1], DownCounter_v1_1_p3[0]
  // pedestrian_button pedestrian_button_1: pin names not known; wires that end beside it: DownCounter_v1_1_p3, pedestrian_button_1_p2
  _7_Segment_Display #(.active("false")) u_7_segment_display_1 (
    .g(HEX1[6]), .f(HEX1[5]), .a(HEX1[0]), .b(HEX1[1]), .e(HEX1[4]), .d(HEX1[3]), .c(HEX1[2]), .dp(HEX1[7]));
  // DownCounter_v1 downcounter_v1_1: pin names not known; wires that end beside it: or_2_out, clk, downcounter_v1_1_p3_2, downcounter_v1_1_p3_2[3], downcounter_v1_1_p3_2[2], downcounter_v1_1_p3_2[1], downcounter_v1_1_p3_2[0]
  // pedestrian_button pedestrian_button_1: pin names not known; wires that end beside it: downcounter_v1_1_p3_2, pedestrian_button_1_p2_2
  _7_Segment_Display #(.active("false")) L_7_Segment_Display_2 (
    .g(HEX0[6]), .f(HEX0[5]), .a(HEX0[0]), .b(HEX0[1]), .e(HEX0[4]), .d(HEX0[3]), .c(HEX0[2]), .dp(HEX0[7]));
  _7_Segment_Display #(.active("false")) u_7_segment_display_2 (
    .g(HEX0[6]), .f(HEX0[5]), .a(HEX0[0]), .b(HEX0[1]), .e(HEX0[4]), .d(HEX0[3]), .c(HEX0[2]), .dp(HEX0[7]));
  // Bin2Hex_2 Bin2Hex_1: pin names not known; wires that end beside it: HEX1, HEX0
  // Bin2Hex_2 bin2hex_2_1: pin names not known; wires that end beside it: HEX1, HEX0
  // RGBLED RGBLED_1: pin names not known; wires that end beside it: R
  // RGBLED RGBLED_2: pin names not known; wires that end beside it: Y, Y
  // RGBLED RGBLED_3: pin names not known; wires that end beside it: G
  Button button_1 (.out(button_1_out));
  // RGBLED rgbled_1: pin names not known; wires that end beside it: RB
  // RGBLED rgbled_2: pin names not known; wires that end beside it: YB, YB
  // RGBLED rgbled_3: pin names not known; wires that end beside it: GB
  _7_Segment_Display #(.active("false")) u_7_segment_display_3 (
    .g(HEX12[6]), .f(HEX12[5]), .a(HEX12[0]), .b(HEX12[1]), .e(HEX12[4]), .d(HEX12[3]), .c(HEX12[2]),
    .dp(HEX12[7]));
  Clock clock_2 (.out(clk));
  _7_Segment_Display #(.active("false")) u_7_segment_display_4 (
    .g(HEX02[6]), .f(HEX02[5]), .a(HEX02[0]), .b(HEX02[1]), .e(HEX02[4]), .d(HEX02[3]), .c(HEX02[2]),
    .dp(HEX02[7]));
  or or_3 (or_3_out, button_1_out, pedestrian_button_2_p2);
  downcount_10_0 downcount_10_0_1 (.en(or_3_out), .clk(clk), .count(downcount_10_0_1_count));
  // pedestrian_button pedestrian_button_2: pin names not known; wires that end beside it: downcount_10_0_1_count, pedestrian_button_2_p2, downcount_10_0_1_count, downcount_10_0_1_count[2], downcount_10_0_1_count[1], downcount_10_0_1_count[0]
  // Bin2Hex_2 bin2hex_2_2: pin names not known; wires that end beside it: downcount_10_0_1_count[3], HEX12, HEX02

  // Notes on the sheet:
  //   Counter Display
  //   Counter Display
  //   Traffic Light A
  //   Traffic Light B
  //   Counter Display
endmodule

module incorp_button2 (
  input  ped_active,
  input  en
);

  wire and_1_out, and_2_out, and_3_out, and_4_out, clk, fsm_light_a_1_g, fsm_light_a_1_r, fsm_light_a_1_y,
       fsm_light_b_1_g, fsm_light_b_1_r, fsm_light_b_1_y, G, GB, multiplexer_1_out, multiplexer_2_out,
       nState, or_1_out, or_2_out, or_3_out, or_10_out, pedestrian_button_1_p2, pedestrian_button_1_p2_2,
       pedestrian_button_2_p2, R, RB, Y, YB;
  wire [3:0] downcount_10_0_1_count, DownCounter_v1_1_p3, downcounter_v1_1_p3_2;
  wire [7:0] HEX0, HEX1, HEX02, HEX12;

  and and_1 (and_1_out, ~DownCounter_v1_1_p3[0], ~DownCounter_v1_1_p3[1], ~DownCounter_v1_1_p3[2], ~DownCounter_v1_1_p3[3]);  // AND_Gate
  Multiplexer multiplexer_1 (.in0(en), .in1(ped_active), .out(multiplexer_1_out), .sel(ped_active));
  and and_2 (and_2_out, en, and_1_out);
  Clock u_clk (.out(clk));
  Multiplexer multiplexer_2 (.in0(en), .in1(ped_active), .out(multiplexer_2_out), .sel(ped_active));
  and and_3 (and_3_out, ~downcounter_v1_1_p3_2[0], ~downcounter_v1_1_p3_2[1], ~downcounter_v1_1_p3_2[2], ~downcounter_v1_1_p3_2[3]);  // AND_Gate
  or or_1 (or_1_out, nState, pedestrian_button_1_p2);
  and and_4 (and_4_out, en, and_3_out);
  Clock clock_1 (.out(clk));
  or or_2 (or_2_out, nState, pedestrian_button_1_p2_2);
  or or_3 (or_3_out, ped_active, fsm_light_a_1_g);
  FSM_Light_A fsm_light_a_1 (
    .en(multiplexer_1_out), .next_state(and_2_out), .G(fsm_light_a_1_g), .Y(fsm_light_a_1_y),
    .R(fsm_light_a_1_r), .rst(nState));
  FSM_Light_B fsm_light_b_1 (
    .en(multiplexer_2_out), .next_state(and_4_out), .G(fsm_light_b_1_g), .Y(fsm_light_b_1_y),
    .R(fsm_light_b_1_r), .rst(nState));
  or or_4 (G, or_3_out, fsm_light_a_1_g);
  // DownCounter_v1 DownCounter_v1_1: pin names not known; wires that end beside it: or_1_out, clk, DownCounter_v1_1_p3, DownCounter_v1_1_p3[3], DownCounter_v1_1_p3[2], DownCounter_v1_1_p3[1], DownCounter_v1_1_p3[0]
  // pedestrian_button pedestrian_button_1: pin names not known; wires that end beside it: DownCounter_v1_1_p3, pedestrian_button_1_p2
  or or_5 (Y, ped_active, fsm_light_a_1_y);
  or or_6 (GB, ped_active, fsm_light_b_1_g);
  // DownCounter_v1 downcounter_v1_1: pin names not known; wires that end beside it: or_2_out, clk, downcounter_v1_1_p3_2, downcounter_v1_1_p3_2[3], downcounter_v1_1_p3_2[2], downcounter_v1_1_p3_2[1], downcounter_v1_1_p3_2[0]
  // pedestrian_button pedestrian_button_1: pin names not known; wires that end beside it: downcounter_v1_1_p3_2, pedestrian_button_1_p2_2
  or or_7 (R, ped_active, fsm_light_a_1_r);
  or or_8 (YB, ped_active, fsm_light_b_1_y);
  // Bin2Hex_2 Bin2Hex_1: pin names not known; wires that end beside it: HEX1, HEX0
  or or_9 (RB, ped_active, fsm_light_b_1_r);
  // Bin2Hex_2 bin2hex_2_1: pin names not known; wires that end beside it: HEX1, HEX0
  // RGBLED RGBLED_1: pin names not known; wires that end beside it: R
  // RGBLED RGBLED_2: pin names not known; wires that end beside it: Y, Y
  // RGBLED RGBLED_3: pin names not known; wires that end beside it: G
  // RGBLED rgbled_1: pin names not known; wires that end beside it: RB
  // RGBLED rgbled_2: pin names not known; wires that end beside it: YB, YB
  // RGBLED rgbled_3: pin names not known; wires that end beside it: GB
  Clock clock_2 (.out(clk));
  or or_10 (or_10_out, ped_active, pedestrian_button_2_p2);
  _7_Segment_Display #(.active("false")) L_7_Segment_Display_1 (
    .g(HEX1[6]), .f(HEX1[5]), .a(HEX1[0]), .b(HEX1[1]), .e(HEX1[4]), .d(HEX1[3]), .c(HEX1[2]), .dp(HEX1[7]));
  _7_Segment_Display #(.active("false")) L_7_Segment_Display_2 (
    .g(HEX0[6]), .f(HEX0[5]), .a(HEX0[0]), .b(HEX0[1]), .e(HEX0[4]), .d(HEX0[3]), .c(HEX0[2]), .dp(HEX0[7]));
  _7_Segment_Display #(.active("false")) u_7_segment_display_1 (
    .g(HEX12[6]), .f(HEX12[5]), .a(HEX12[0]), .b(HEX12[1]), .e(HEX12[4]), .d(HEX12[3]), .c(HEX12[2]),
    .dp(HEX12[7]));
  downcount_10_0 downcount_10_0_1 (.en(or_10_out), .clk(clk), .count(downcount_10_0_1_count));
  // pedestrian_button pedestrian_button_2: pin names not known; wires that end beside it: downcount_10_0_1_count, pedestrian_button_2_p2, downcount_10_0_1_count[2], downcount_10_0_1_count[1], downcount_10_0_1_count[0]
  _7_Segment_Display #(.active("false")) u_7_segment_display_2 (
    .g(HEX1[6]), .f(HEX1[5]), .a(HEX1[0]), .b(HEX1[1]), .e(HEX1[4]), .d(HEX1[3]), .c(HEX1[2]), .dp(HEX1[7]));
  _7_Segment_Display #(.active("false")) u_7_segment_display_3 (
    .g(HEX02[6]), .f(HEX02[5]), .a(HEX02[0]), .b(HEX02[1]), .e(HEX02[4]), .d(HEX02[3]), .c(HEX02[2]),
    .dp(HEX02[7]));
  _7_Segment_Display #(.active("false")) u_7_segment_display_4 (
    .g(HEX0[6]), .f(HEX0[5]), .a(HEX0[0]), .b(HEX0[1]), .e(HEX0[4]), .d(HEX0[3]), .c(HEX0[2]), .dp(HEX0[7]));
  // Bin2Hex_2 bin2hex_2_2: pin names not known; wires that end beside it: downcount_10_0_1_count[3], HEX12, HEX02

  // Other names for the same wires on the sheet: PA = ped_active

  // Notes on the sheet:
  //   Traffic Light A
  //   Traffic Light B
  //   Counter Display A
  //   Crosswalk
  //   Counter Display B
endmodule

module incopr_button3 (
  input  ped_active,
  input  en
);

  wire and_1_out, and_2_out, and_3_out, and_4_out, clk, fsm_light_a_1_r, fsm_light_b_1_r, G, GB,
       multiplexer_1_out, multiplexer_2_out, nState, or_1_out, or_2_out, or_5_out, pedestrian_button_1_p2,
       pedestrian_button_1_p2_2, pedestrian_button_2_p2, R, RB, Y, YB;
  wire [3:0] downcount_10_0_1_count, DownCounter_v1_1_p3, downcounter_v1_1_p3_2;
  wire [7:0] HEX0, HEX1, HEX02, HEX12;

  and and_1 (and_1_out, ~DownCounter_v1_1_p3[0], ~DownCounter_v1_1_p3[1], ~DownCounter_v1_1_p3[2], ~DownCounter_v1_1_p3[3]);  // AND_Gate
  // Switch switch_1: pin names not known
  Multiplexer multiplexer_1 (.in0(en), .in1(ped_active), .out(multiplexer_1_out), .sel(ped_active));
  and and_2 (and_2_out, en, and_1_out);
  Clock u_clk (.out(clk));
  Multiplexer multiplexer_2 (.in0(en), .in1(ped_active), .out(multiplexer_2_out), .sel(ped_active));
  and and_3 (and_3_out, ~downcounter_v1_1_p3_2[0], ~downcounter_v1_1_p3_2[1], ~downcounter_v1_1_p3_2[2], ~downcounter_v1_1_p3_2[3]);  // AND_Gate
  Clock clock_1 (.out(clk));
  or or_1 (or_1_out, nState, pedestrian_button_1_p2);
  and and_4 (and_4_out, en, and_3_out);
  or or_2 (or_2_out, nState, pedestrian_button_1_p2_2);
  FSM_Light_A fsm_light_a_1 (
    .en(multiplexer_1_out), .next_state(and_2_out), .G(G), .Y(Y), .R(fsm_light_a_1_r), .rst(nState));
  FSM_Light_B fsm_light_b_1 (
    .en(multiplexer_2_out), .next_state(and_4_out), .G(GB), .Y(YB), .R(fsm_light_b_1_r), .rst(nState));
  // DownCounter_v1 DownCounter_v1_1: pin names not known; wires that end beside it: or_1_out, clk, DownCounter_v1_1_p3, DownCounter_v1_1_p3[3], DownCounter_v1_1_p3[2], DownCounter_v1_1_p3[1], DownCounter_v1_1_p3[0]
  // pedestrian_button pedestrian_button_1: pin names not known; wires that end beside it: DownCounter_v1_1_p3, pedestrian_button_1_p2
  // DownCounter_v1 downcounter_v1_1: pin names not known; wires that end beside it: or_2_out, clk, downcounter_v1_1_p3_2, downcounter_v1_1_p3_2[3], downcounter_v1_1_p3_2[2], downcounter_v1_1_p3_2[1], downcounter_v1_1_p3_2[0]
  // pedestrian_button pedestrian_button_1: pin names not known; wires that end beside it: downcounter_v1_1_p3_2, pedestrian_button_1_p2_2
  or or_3 (R, ped_active, fsm_light_a_1_r);
  // Bin2Hex_2 Bin2Hex_1: pin names not known; wires that end beside it: HEX1, HEX0
  or or_4 (RB, ped_active, fsm_light_b_1_r);
  // Bin2Hex_2 bin2hex_2_1: pin names not known; wires that end beside it: HEX1, HEX0
  // RGBLED RGBLED_1: pin names not known; wires that end beside it: R
  // RGBLED RGBLED_2: pin names not known; wires that end beside it: Y, Y
  // RGBLED RGBLED_3: pin names not known; wires that end beside it: G
  // RGBLED rgbled_1: pin names not known; wires that end beside it: RB
  // RGBLED rgbled_2: pin names not known; wires that end beside it: YB, YB
  // RGBLED rgbled_3: pin names not known; wires that end beside it: GB
  Clock clock_2 (.out(clk));
  or or_5 (or_5_out, ped_active, pedestrian_button_2_p2);
  _7_Segment_Display #(.active("false")) L_7_Segment_Display_1 (
    .g(HEX1[6]), .f(HEX1[5]), .a(HEX1[0]), .b(HEX1[1]), .e(HEX1[4]), .d(HEX1[3]), .c(HEX1[2]), .dp(HEX1[7]));
  _7_Segment_Display #(.active("false")) L_7_Segment_Display_2 (
    .g(HEX0[6]), .f(HEX0[5]), .a(HEX0[0]), .b(HEX0[1]), .e(HEX0[4]), .d(HEX0[3]), .c(HEX0[2]), .dp(HEX0[7]));
  _7_Segment_Display #(.active("false")) u_7_segment_display_1 (
    .g(HEX12[6]), .f(HEX12[5]), .a(HEX12[0]), .b(HEX12[1]), .e(HEX12[4]), .d(HEX12[3]), .c(HEX12[2]),
    .dp(HEX12[7]));
  downcount_10_0 downcount_10_0_1 (.en(or_5_out), .clk(clk), .count(downcount_10_0_1_count));
  // pedestrian_button pedestrian_button_2: pin names not known; wires that end beside it: downcount_10_0_1_count, pedestrian_button_2_p2, downcount_10_0_1_count[2], downcount_10_0_1_count[1], downcount_10_0_1_count[0]
  _7_Segment_Display #(.active("false")) u_7_segment_display_2 (
    .g(HEX02[6]), .f(HEX02[5]), .a(HEX02[0]), .b(HEX02[1]), .e(HEX02[4]), .d(HEX02[3]), .c(HEX02[2]),
    .dp(HEX02[7]));
  _7_Segment_Display #(.active("false")) u_7_segment_display_3 (
    .g(HEX1[6]), .f(HEX1[5]), .a(HEX1[0]), .b(HEX1[1]), .e(HEX1[4]), .d(HEX1[3]), .c(HEX1[2]), .dp(HEX1[7]));
  _7_Segment_Display #(.active("false")) u_7_segment_display_4 (
    .g(HEX0[6]), .f(HEX0[5]), .a(HEX0[0]), .b(HEX0[1]), .e(HEX0[4]), .d(HEX0[3]), .c(HEX0[2]), .dp(HEX0[7]));
  // Bin2Hex_2 bin2hex_2_2: pin names not known; wires that end beside it: downcount_10_0_1_count[3], HEX12, HEX02

  // Other names for the same wires on the sheet: PA = ped_active

  // Notes on the sheet:
  //   Traffic Light A
  //   Traffic Light B
  //   Counter Display A
  //   Crosswalk
  //   Counter Display B
endmodule

module Global_FSM_lights (
  input  en,
  input  next_state,
  output GB,
  output YB,
  output RB,
  output rst,
  output GA,
  output YA,
  output RA
);

  wire and_3_out, and_4_out, and_7_out, and_8_out;
  wire [1:0] multiplexer_1_out, multiplexer_2_out, register_1_q, register_2_q;

  Multiplexer #(.select(3), .width(2)) multiplexer_1 (
    .in0(2'b00), .in1(2'b01), .in2(2'b10), .in3(2'b11), .in4(2'b01), .in5(2'b10), .in6(2'b11), .in7(2'b00),
    .out(multiplexer_1_out), .sel({en, register_1_q}));
  // Probe on multiplexer_1_out
  Multiplexer #(.select(3), .width(2)) multiplexer_2 (
    .in0(2'b00), .in1(2'b01), .in2(2'b10), .in3(2'b11), .in4(2'b01), .in5(2'b10), .in6(2'b11), .in7(2'b00),
    .out(multiplexer_2_out), .sel({en, register_2_q}));
  Register #(.width(2)) register_1 (.D(multiplexer_1_out), .Q(register_1_q), .clk(next_state));  // open: en, clr
  // Probe on multiplexer_2_out
  // Probe on register_1_q
  Register #(.width(2)) register_2 (.D(multiplexer_2_out), .Q(register_2_q), .clk(next_state));  // open: en, clr
  // Probe on register_2_q
  and and_1 (GB, ~register_1_q[0], ~register_1_q[1]);  // AND_Gate
  and and_2 (YB, register_1_q[0], ~register_1_q[1]);  // AND_Gate
  and and_3 (and_3_out, ~register_1_q[0], register_1_q[1]);  // AND_Gate
  and and_4 (and_4_out, register_1_q[0], register_1_q[1]);
  and and_5 (GA, ~register_2_q[0], register_2_q[1]);  // AND_Gate
  and and_6 (YA, register_2_q[0], register_2_q[1]);
  or or_1 (RB, and_3_out, and_4_out);
  and and_7 (and_7_out, ~register_2_q[0], ~register_2_q[1]);  // AND_Gate
  and and_8 (and_8_out, register_2_q[0], ~register_2_q[1]);  // AND_Gate
  or or_2 (RA, and_7_out, and_8_out);

  assign rst = next_state;

  // Notes on the sheet:
  //   Light B
  //   Light A
endmodule

module test_GLOBALFSM (
  input  en
);

  wire and_1_out, and_2_out, clk, G, GB, nState, or_1_out, pedestrian_button_1_p2, R, RB, Y, YB;
  wire [3:0] DownCounter_v1_1_p3;
  wire [7:0] HEX0, HEX1;

  and and_1 (and_1_out, ~DownCounter_v1_1_p3[0], ~DownCounter_v1_1_p3[1], ~DownCounter_v1_1_p3[2], ~DownCounter_v1_1_p3[3]);  // AND_Gate
  Clock u_clk (.out(clk));
  and and_2 (and_2_out, en, and_1_out);
  or or_1 (or_1_out, nState, pedestrian_button_1_p2);
  FSMGLobal_Button_3bit fsmglobal_button_3bit_1 (
    .en(en), .next_state(and_2_out), .GB(GB), .YB(YB), .RB(RB), .rst(nState), .GA(G), .YA(Y), .RA(R));
  // DownCounter_v1 DownCounter_v1_1: pin names not known; wires that end beside it: or_1_out, clk, DownCounter_v1_1_p3, DownCounter_v1_1_p3[3], DownCounter_v1_1_p3[2], DownCounter_v1_1_p3[1], DownCounter_v1_1_p3[0]
  // pedestrian_button pedestrian_button_1: pin names not known; wires that end beside it: DownCounter_v1_1_p3, pedestrian_button_1_p2
  // Bin2Hex_2 Bin2Hex_1: pin names not known; wires that end beside it: HEX1, HEX0
  // RGBLED RGBLED_1: pin names not known; wires that end beside it: R
  // RGBLED RGBLED_2: pin names not known; wires that end beside it: Y, Y
  // RGBLED RGBLED_3: pin names not known; wires that end beside it: G
  // RGBLED rgbled_1: pin names not known; wires that end beside it: RB
  // RGBLED rgbled_2: pin names not known; wires that end beside it: YB, YB
  // RGBLED rgbled_3: pin names not known; wires that end beside it: GB
  _7_Segment_Display #(.active("false")) L_7_Segment_Display_1 (
    .g(HEX1[6]), .f(HEX1[5]), .a(HEX1[0]), .b(HEX1[1]), .e(HEX1[4]), .d(HEX1[3]), .c(HEX1[2]), .dp(HEX1[7]));
  _7_Segment_Display #(.active("false")) L_7_Segment_Display_2 (
    .g(HEX0[6]), .f(HEX0[5]), .a(HEX0[0]), .b(HEX0[1]), .e(HEX0[4]), .d(HEX0[3]), .c(HEX0[2]), .dp(HEX0[7]));

  // Notes on the sheet:
  //   Traffic Light A
  //   Traffic Light B
  //   Counter_3sec
endmodule

module FSMGLobal_Button_3bit (
  input  en,
  input  next_state,
  output GB,
  output YB,
  output RB,
  output rst,
  output GA,
  output YA,
  output RA
);

  wire and_3_out, and_4_out, and_7_out, and_8_out;
  wire [1:0] register_1_q, register_2_q;
  wire [2:0] multiplexer_1_out, multiplexer_2_out;
  wire [2:2] register_1_q_2, register_2_q_2;

  Multiplexer #(.select(3), .width(3)) multiplexer_1 (
    .in0(3'b000), .in1(3'b001), .in2(3'b010), .in3(3'b011), .in4(3'b001), .in5(3'b010), .in6(3'b011),
    .in7(3'b000), .out(multiplexer_1_out), .sel({en, register_1_q}));
  // Probe on multiplexer_1_out
  Multiplexer #(.select(3), .width(3)) multiplexer_2 (
    .in0(3'b000), .in1(3'b001), .in2(3'b010), .in3(3'b011), .in4(3'b001), .in5(3'b010), .in6(3'b011),
    .in7(3'b000), .out(multiplexer_2_out), .sel({en, register_2_q}));
  Register #(.width(3)) register_1 (
    .D(multiplexer_1_out), .Q({register_1_q_2[2], register_1_q}), .clk(next_state));  // open: en, clr
  // Probe on multiplexer_2_out
  // Probe on {register_1_q_2[2], register_1_q}
  Register #(.width(3)) register_2 (
    .D(multiplexer_2_out), .Q({register_2_q_2[2], register_2_q}), .clk(next_state));  // open: en, clr
  // Probe on {register_2_q_2[2], register_2_q}
  and and_1 (GB, ~register_1_q[0], ~register_1_q[1]);  // AND_Gate
  and and_2 (YB, register_1_q[0], ~register_1_q[1]);  // AND_Gate
  and and_3 (and_3_out, ~register_1_q[0], register_1_q[1]);  // AND_Gate
  and and_4 (and_4_out, register_1_q[0], register_1_q[1]);
  and and_5 (GA, ~register_2_q[0], register_2_q[1]);  // AND_Gate
  and and_6 (YA, register_2_q[0], register_2_q[1]);
  or or_1 (RB, and_3_out, and_4_out);
  and and_7 (and_7_out, ~register_2_q[0], ~register_2_q[1]);  // AND_Gate
  and and_8 (and_8_out, register_2_q[0], ~register_2_q[1]);  // AND_Gate
  or or_2 (RA, and_7_out, and_8_out);

  assign rst = next_state;

  // Notes on the sheet:
  //   Light B
  //   Light A
endmodule

module ped_fsm_fail (
  input  ped_active,
  output RB,
  output RA,
  output off
);

  not not_1 (off, ped_active);

  assign RA = ped_active;
  assign RB = ped_active;

  // Other names for the same wires on the sheet: PA2 = ped_active
endmodule

module test123 (
  input  in_1,
  input  ped_active,
  input  en
);

  wire and_1_out, and_2_out, and_3_out, clk, full_fsm_1_g_off, full_fsm_1_ga, full_fsm_1_gb, full_fsm_1_r_on,
       full_fsm_1_ra, full_fsm_1_rb, full_fsm_1_y_off, full_fsm_1_ya, full_fsm_1_yb, G, GB, nState, or_1_out,
       or_8_out, pedestrian_button_1_p2, pedestrian_button_1_p3, R, RB, Y, YB;
  wire [3:0] downcount_10_0_1_count, DownCounter_v1_1_p3;
  wire [7:0] HEX0, HEX0C, HEX1, HEX1C;

  Button button_1 ();  // open: out
  and and_1 (and_1_out, ~DownCounter_v1_1_p3[0], ~DownCounter_v1_1_p3[1], ~DownCounter_v1_1_p3[2], ~DownCounter_v1_1_p3[3]);  // AND_Gate
  and and_2 (and_2_out, en, and_1_out);
  Clock u_clk (.out(clk));
  Multiplexer multiplexer_1 (.sel(in_1));  // open: in0, in1, out
  or or_1 (or_1_out, nState, pedestrian_button_1_p2);
  FULL_FSM full_fsm_1 (
    .ped_active(ped_active), .en(en), .next_state(and_2_out), .G_off(full_fsm_1_g_off),
    .Y_off(full_fsm_1_y_off), .R_on(full_fsm_1_r_on), .GB(full_fsm_1_gb), .YB(full_fsm_1_yb),
    .RB(full_fsm_1_rb), .rst(nState), .GA(full_fsm_1_ga), .YA(full_fsm_1_ya), .RA(full_fsm_1_ra));
  // DownCounter_v1 DownCounter_v1_1: pin names not known; wires that end beside it: or_1_out, clk, DownCounter_v1_1_p3, DownCounter_v1_1_p3[3], DownCounter_v1_1_p3[2], DownCounter_v1_1_p3[1], DownCounter_v1_1_p3[0]
  // pedestrian_button pedestrian_button_1: pin names not known; wires that end beside it: DownCounter_v1_1_p3, pedestrian_button_1_p2
  or or_2 (GB, full_fsm_1_g_off, full_fsm_1_gb);
  or or_3 (YB, full_fsm_1_y_off, full_fsm_1_yb);
  or or_4 (RB, full_fsm_1_r_on, full_fsm_1_rb);
  or or_5 (G, full_fsm_1_ga, full_fsm_1_g_off);
  or or_6 (Y, full_fsm_1_ya, full_fsm_1_y_off);
  or or_7 (R, full_fsm_1_ra, full_fsm_1_r_on);
  // Bin2Hex_2 Bin2Hex_1: pin names not known; wires that end beside it: HEX1, HEX0
  // RGBLED RGBLED_1: pin names not known; wires that end beside it: R
  // RGBLED RGBLED_2: pin names not known; wires that end beside it: Y, Y
  // RGBLED RGBLED_3: pin names not known; wires that end beside it: G
  _7_Segment_Display #(.active("false")) u_7_segment_display_1 (
    .g(HEX1C[6]), .f(HEX1C[5]), .a(HEX1C[0]), .b(HEX1C[1]), .e(HEX1C[4]), .d(HEX1C[3]), .c(HEX1C[2]),
    .dp(HEX1C[7]));
  Clock clock_1 (.out(clk));
  _7_Segment_Display #(.active("false")) u_7_segment_display_2 (
    .g(HEX0C[6]), .f(HEX0C[5]), .a(HEX0C[0]), .b(HEX0C[1]), .e(HEX0C[4]), .d(HEX0C[3]), .c(HEX0C[2]),
    .dp(HEX0C[7]));
  or or_8 (or_8_out, ped_active, pedestrian_button_1_p3);
  // RGBLED rgbled_1: pin names not known; wires that end beside it: RB
  // RGBLED rgbled_2: pin names not known; wires that end beside it: YB, YB
  // RGBLED rgbled_3: pin names not known; wires that end beside it: GB
  _7_Segment_Display #(.active("false")) L_7_Segment_Display_1 (
    .g(HEX1[6]), .f(HEX1[5]), .a(HEX1[0]), .b(HEX1[1]), .e(HEX1[4]), .d(HEX1[3]), .c(HEX1[2]), .dp(HEX1[7]));
  and and_3 (and_3_out, ~downcount_10_0_1_count[0], ~downcount_10_0_1_count[1], ~downcount_10_0_1_count[2], ~downcount_10_0_1_count[3]);  // AND_Gate
  downcount_10_0 downcount_10_0_1 (.en(or_8_out), .clk(clk), .count(downcount_10_0_1_count));
  // pedestrian_button pedestrian_button_1: pin names not known; wires that end beside it: downcount_10_0_1_count, and_3_out, pedestrian_button_1_p3, downcount_10_0_1_count[2], downcount_10_0_1_count[1], downcount_10_0_1_count[0]
  _7_Segment_Display #(.active("false")) L_7_Segment_Display_2 (
    .g(HEX0[6]), .f(HEX0[5]), .a(HEX0[0]), .b(HEX0[1]), .e(HEX0[4]), .d(HEX0[3]), .c(HEX0[2]), .dp(HEX0[7]));
  // Bin2Hex_2 bin2hex_2_1: pin names not known; wires that end beside it: downcount_10_0_1_count[3], HEX1C, HEX0C

  // Other names for the same wires on the sheet: PA = ped_active

  // Notes on the sheet:
  //   Traffic Light A
  //   Counter Display
  //   Traffic Light B
  //   Counter_3sec
endmodule

module FULL_FSM (
  input  ped_active,
  input  en,
  input  next_state,
  output G_off,
  output Y_off,
  output R_on,
  output GB,
  output YB,
  output RB,
  output rst,
  output GA,
  output YA,
  output RA
);

  wire and_6_out, and_7_out, and_10_out, and_11_out;
  wire [2:0] multiplexer_1_out, multiplexer_2_out, multiplexer_3_out, register_1_q, register_2_q,
       register_3_q;
  wire [2:1] undriven;

  Multiplexer #(.width(3)) multiplexer_1 (
    .in0({undriven, en}), .in1(3'b100), .out(multiplexer_1_out), .sel(ped_active));
  Register #(.width(3)) register_1 (.D(multiplexer_1_out), .Q(register_1_q), .clk(next_state));  // open: en, clr
  Multiplexer #(.enable("true"), .select(3), .width(3)) multiplexer_2 (
    .in0(3'b000), .in1(3'b001), .in2(3'b010), .in3(3'b011), .in4(3'b001), .in5(3'b010), .in6(3'b011),
    .in7(3'b000), .out(multiplexer_2_out), .sel({en, register_2_q[1:0]}));  // open: en
  // Probe on multiplexer_2_out
  Multiplexer #(.enable("true"), .select(3), .width(3)) multiplexer_3 (
    .in0(3'b000), .in1(3'b001), .in2(3'b010), .in3(3'b011), .in4(3'b001), .in5(3'b010), .in6(3'b011),
    .in7(3'b000), .out(multiplexer_3_out), .sel({en, register_3_q[1:0]}));  // open: en
  Register #(.width(3)) register_2 (.D(multiplexer_2_out), .Q(register_2_q), .clk(next_state));  // open: en, clr
  // Probe on register_2_q
  // Probe on multiplexer_3_out
  Register #(.width(3)) register_3 (.D(multiplexer_3_out), .Q(register_3_q), .clk(next_state));  // open: en, clr
  and and_1 (G_off, register_1_q[0], register_1_q[1]);
  and and_2 (Y_off, register_1_q[0], register_1_q[1]);
  and and_3 (R_on, ~register_1_q[0], ~register_1_q[1]);  // AND_Gate
  // Probe on register_3_q
  and and_4 (GB, ~register_2_q[0], ~register_2_q[1]);  // AND_Gate
  and and_5 (YB, register_2_q[0], ~register_2_q[1]);  // AND_Gate
  and and_6 (and_6_out, ~register_2_q[0], register_2_q[1]);  // AND_Gate
  and and_7 (and_7_out, register_2_q[0], register_2_q[1]);
  and and_8 (GA, ~register_3_q[0], register_3_q[1]);  // AND_Gate
  and and_9 (YA, register_3_q[0], register_3_q[1]);
  and and_10 (and_10_out, ~register_3_q[0], ~register_3_q[1]);  // AND_Gate
  and and_11 (and_11_out, register_3_q[0], ~register_3_q[1]);  // AND_Gate
  or or_1 (RB, and_6_out, and_7_out);
  or or_2 (RA, and_10_out, and_11_out);

  assign rst = next_state;

  // Notes on the sheet:
  //   Light B
  //   Light A
endmodule

module full2fsm (
  input  ped_active,
  input  nxt2,
  input  enable,
  input  next_state,
  output G_off,
  output Y_off,
  output R_on,
  output rst2,
  output GB,
  output YB,
  output RB,
  output rst,
  output GA,
  output YA,
  output RA
);

  wire and_6_out, and_7_out, and_10_out, and_11_out;
  wire [2:0] multiplexer_1_out, multiplexer_2_out, multiplexer_3_out, register_1_q, register_2_q,
       register_3_q, undriven;

  Multiplexer #(.width(3)) multiplexer_1 (
    .in0({undriven[2], enable, undriven[0]}), .in1(3'b100), .out(multiplexer_1_out), .sel(ped_active));
  Register #(.width(3)) register_1 (.D(multiplexer_1_out), .Q(register_1_q), .clk(nxt2));  // open: en, clr
  Multiplexer #(.select(3), .width(3)) multiplexer_2 (
    .in0(3'b000), .in1(3'b001), .in2(3'b010), .in3(3'b011), .in4(3'b001), .in5(3'b010), .in6(3'b011),
    .in7(3'b000), .out(multiplexer_2_out), .sel({enable, register_2_q[1:0]}));
  // Probe on multiplexer_2_out
  Multiplexer #(.select(3), .width(3)) multiplexer_3 (
    .in0(3'b000), .in1(3'b001), .in2(3'b010), .in3(3'b011), .in4(3'b001), .in5(3'b010), .in6(3'b011),
    .in7(3'b000), .out(multiplexer_3_out), .sel({enable, register_3_q[1:0]}));
  Register #(.width(3)) register_2 (.D(multiplexer_2_out), .Q(register_2_q), .clk(next_state));  // open: en, clr
  // Probe on register_2_q
  // Probe on multiplexer_3_out
  Register #(.width(3)) register_3 (.D(multiplexer_3_out), .Q(register_3_q), .clk(next_state));  // open: en, clr
  and and_1 (G_off, register_1_q[0], register_1_q[1]);
  and and_2 (Y_off, register_1_q[0], register_1_q[1]);
  and and_3 (R_on, ~register_1_q[0], ~register_1_q[1]);  // AND_Gate
  // Probe on register_3_q
  and and_4 (GB, ~register_2_q[0], ~register_2_q[1]);  // AND_Gate
  and and_5 (YB, register_2_q[0], ~register_2_q[1]);  // AND_Gate
  and and_6 (and_6_out, ~register_2_q[0], register_2_q[1]);  // AND_Gate
  and and_7 (and_7_out, register_2_q[0], register_2_q[1]);
  and and_8 (GA, ~register_3_q[0], register_3_q[1]);  // AND_Gate
  and and_9 (YA, register_3_q[0], register_3_q[1]);
  and and_10 (and_10_out, ~register_3_q[0], ~register_3_q[1]);  // AND_Gate
  and and_11 (and_11_out, register_3_q[0], ~register_3_q[1]);  // AND_Gate
  or or_1 (RB, and_6_out, and_7_out);
  or or_2 (RA, and_10_out, and_11_out);

  assign rst = next_state;
  assign rst2 = nxt2;

  // Notes on the sheet:
  //   Light B
  //   Light A
endmodule

module trial400 (
  input  ped_active,
  input  en
);

  wire and_1_out, and_2_out, and_3_out, and_4_out, clk, full2fsm_1_g_off, full2fsm_1_ga, full2fsm_1_gb,
       full2fsm_1_r_on, full2fsm_1_ra, full2fsm_1_rb, full2fsm_1_y_off, full2fsm_1_ya, full2fsm_1_yb, G, GB,
       nState, or_1_out, or_8_out, PA_nstate, pedestrian_button_1_p2, pedestrian_button_1_p2_2, R, RB,
       undriven, Y, YB;
  wire [3:0] downcount_10_0_1_count, DownCounter_v1_1_p3;
  wire [7:0] HEX0, HEX0C, HEX1, HEX1C;

  Button button_1 ();  // open: out
  and and_1 (and_1_out, en, and_2_out);
  and and_2 (and_2_out, ~DownCounter_v1_1_p3[0], ~DownCounter_v1_1_p3[1], ~DownCounter_v1_1_p3[2], ~DownCounter_v1_1_p3[3]);  // AND_Gate
  Clock u_clk (.out(clk));
  or or_1 (or_1_out, nState, pedestrian_button_1_p2);
  full2fsm full2fsm_1 (
    .ped_active(ped_active), .nxt2(and_4_out), .enable(and_1_out), .next_state(en), .G_off(full2fsm_1_g_off),
    .Y_off(full2fsm_1_y_off), .R_on(full2fsm_1_r_on), .rst2(PA_nstate), .GB(full2fsm_1_gb),
    .YB(full2fsm_1_yb), .RB(full2fsm_1_rb), .rst(nState), .GA(full2fsm_1_ga), .YA(full2fsm_1_ya),
    .RA(full2fsm_1_ra));
  // DownCounter_v1 DownCounter_v1_1: pin names not known; wires that end beside it: or_1_out, clk, DownCounter_v1_1_p3, DownCounter_v1_1_p3[3], DownCounter_v1_1_p3[2], DownCounter_v1_1_p3[1], DownCounter_v1_1_p3[0]
  // pedestrian_button pedestrian_button_1: pin names not known; wires that end beside it: DownCounter_v1_1_p3, pedestrian_button_1_p2
  or or_2 (GB, full2fsm_1_g_off, full2fsm_1_gb);
  or or_3 (YB, full2fsm_1_y_off, full2fsm_1_yb);
  or or_4 (RB, full2fsm_1_r_on, full2fsm_1_rb);
  or or_5 (G, full2fsm_1_g_off, full2fsm_1_ga);
  or or_6 (Y, full2fsm_1_ya, full2fsm_1_y_off);
  or or_7 (R, full2fsm_1_ra, full2fsm_1_r_on);
  // Bin2Hex_2 Bin2Hex_1: pin names not known; wires that end beside it: HEX1, HEX0
  // RGBLED RGBLED_1: pin names not known; wires that end beside it: R
  // RGBLED RGBLED_2: pin names not known; wires that end beside it: Y, Y
  // RGBLED RGBLED_3: pin names not known; wires that end beside it: G
  _7_Segment_Display #(.active("false")) u_7_segment_display_1 (
    .g(HEX1C[6]), .f(HEX1C[5]), .a(HEX1C[0]), .b(HEX1C[1]), .e(HEX1C[4]), .d(HEX1C[3]), .c(HEX1C[2]),
    .dp(HEX1C[7]));
  Clock clock_1 (.out(clk));
  _7_Segment_Display #(.active("false")) u_7_segment_display_2 (
    .g(HEX0C[6]), .f(HEX0C[5]), .a(HEX0C[0]), .b(HEX0C[1]), .e(HEX0C[4]), .d(HEX0C[3]), .c(HEX0C[2]),
    .dp(HEX0C[7]));
  or or_8 (or_8_out, PA_nstate, pedestrian_button_1_p2_2);
  // RGBLED rgbled_1: pin names not known; wires that end beside it: RB
  // RGBLED rgbled_2: pin names not known; wires that end beside it: YB, YB
  // RGBLED rgbled_3: pin names not known; wires that end beside it: GB
  _7_Segment_Display #(.active("false")) L_7_Segment_Display_1 (
    .g(HEX1[6]), .f(HEX1[5]), .a(HEX1[0]), .b(HEX1[1]), .e(HEX1[4]), .d(HEX1[3]), .c(HEX1[2]), .dp(HEX1[7]));
  downcount_10_0 downcount_10_0_1 (.en(or_8_out), .clk(clk), .count(downcount_10_0_1_count));
  // pedestrian_button pedestrian_button_1: pin names not known; wires that end beside it: downcount_10_0_1_count, pedestrian_button_1_p2_2, downcount_10_0_1_count[2], downcount_10_0_1_count[1], downcount_10_0_1_count[0]
  _7_Segment_Display #(.active("false")) L_7_Segment_Display_2 (
    .g(HEX0[6]), .f(HEX0[5]), .a(HEX0[0]), .b(HEX0[1]), .e(HEX0[4]), .d(HEX0[3]), .c(HEX0[2]), .dp(HEX0[7]));
  and and_3 (and_3_out, ~downcount_10_0_1_count[0], ~downcount_10_0_1_count[1], ~downcount_10_0_1_count[2], ~downcount_10_0_1_count[3]);  // AND_Gate
  and and_4 (and_4_out, undriven, and_3_out);
  // Bin2Hex_2 bin2hex_2_1: pin names not known; wires that end beside it: downcount_10_0_1_count[3], HEX1C, HEX0C

  // Other names for the same wires on the sheet: PA = ped_active

  // Notes on the sheet:
  //   Traffic Light A
  //   Counter Display
  //   Traffic Light B
  //   Counter_3sec
endmodule

module CLOSEST_ATTEMPT (
  input  ped_active,
  input  en
);

  wire and_1_out, and_2_out, and_3_out, and_4_out, and_5_out, clk, full_fsm_1_g_off, full_fsm_1_ga,
       full_fsm_1_gb, full_fsm_1_r_on, full_fsm_1_ra, full_fsm_1_rb, full_fsm_1_y_off, full_fsm_1_ya,
       full_fsm_1_yb, G, GB, nState, or_1_out, or_2_out, or_9_out, pedestrian_button_1_p2,
       pedestrian_button_1_p6, R, RB, Y, YB;
  wire [3:0] downcount_10_0_1_count, DownCounter_v1_1_p3;
  wire [7:0] HEX0, HEX0C, HEX1, HEX1C;

  and and_1 (and_1_out, and_5_out, ped_active);
  and and_2 (and_2_out, en, and_3_out);
  and and_3 (and_3_out, ~DownCounter_v1_1_p3[0], ~DownCounter_v1_1_p3[1], ~DownCounter_v1_1_p3[2], ~DownCounter_v1_1_p3[3]);  // AND_Gate
  Clock u_clk (.out(clk));
  or or_1 (or_1_out, and_1_out, and_2_out);
  or or_2 (or_2_out, nState, pedestrian_button_1_p2);
  FULL_FSM full_fsm_1 (
    .ped_active(ped_active), .en(en), .next_state(or_1_out), .G_off(full_fsm_1_g_off),
    .Y_off(full_fsm_1_y_off), .R_on(full_fsm_1_r_on), .GB(full_fsm_1_gb), .YB(full_fsm_1_yb),
    .RB(full_fsm_1_rb), .rst(nState), .GA(full_fsm_1_ga), .YA(full_fsm_1_ya), .RA(full_fsm_1_ra));
  // DownCounter_v1 DownCounter_v1_1: pin names not known; wires that end beside it: or_2_out, clk, DownCounter_v1_1_p3, DownCounter_v1_1_p3[3], DownCounter_v1_1_p3[2], DownCounter_v1_1_p3[1], DownCounter_v1_1_p3[0]
  // pedestrian_button pedestrian_button_1: pin names not known; wires that end beside it: DownCounter_v1_1_p3, pedestrian_button_1_p2
  or or_3 (GB, full_fsm_1_g_off, full_fsm_1_gb);
  or or_4 (YB, full_fsm_1_y_off, full_fsm_1_yb);
  or or_5 (RB, full_fsm_1_r_on, full_fsm_1_rb);
  or or_6 (G, full_fsm_1_ga, full_fsm_1_g_off);
  or or_7 (Y, full_fsm_1_ya, full_fsm_1_y_off);
  or or_8 (R, full_fsm_1_ra, full_fsm_1_r_on);
  // Bin2Hex_2 Bin2Hex_1: pin names not known; wires that end beside it: HEX1, HEX0
  and and_4 (and_4_out, nState, ped_active);
  // RGBLED RGBLED_1: pin names not known; wires that end beside it: R
  // RGBLED RGBLED_2: pin names not known; wires that end beside it: Y, Y
  // RGBLED RGBLED_3: pin names not known; wires that end beside it: G
  _7_Segment_Display #(.active("false")) u_7_segment_display_1 (
    .g(HEX1C[6]), .f(HEX1C[5]), .a(HEX1C[0]), .b(HEX1C[1]), .e(HEX1C[4]), .d(HEX1C[3]), .c(HEX1C[2]),
    .dp(HEX1C[7]));
  Clock clock_1 (.out(clk));
  _7_Segment_Display #(.active("false")) u_7_segment_display_2 (
    .g(HEX0C[6]), .f(HEX0C[5]), .a(HEX0C[0]), .b(HEX0C[1]), .e(HEX0C[4]), .d(HEX0C[3]), .c(HEX0C[2]),
    .dp(HEX0C[7]));
  or or_9 (or_9_out, and_4_out, pedestrian_button_1_p6);
  // RGBLED rgbled_1: pin names not known; wires that end beside it: RB
  // RGBLED rgbled_2: pin names not known; wires that end beside it: YB, YB
  // RGBLED rgbled_3: pin names not known; wires that end beside it: GB
  _7_Segment_Display #(.active("false")) L_7_Segment_Display_1 (
    .g(HEX1[6]), .f(HEX1[5]), .a(HEX1[0]), .b(HEX1[1]), .e(HEX1[4]), .d(HEX1[3]), .c(HEX1[2]), .dp(HEX1[7]));
  and and_5 (and_5_out, ~downcount_10_0_1_count[0], ~downcount_10_0_1_count[1], ~downcount_10_0_1_count[2], ~downcount_10_0_1_count[3]);  // AND_Gate
  downcount_10_0 downcount_10_0_1 (.en(or_9_out), .clk(clk), .count(downcount_10_0_1_count));
  // pedestrian_button pedestrian_button_1: pin names not known; wires that end beside it: downcount_10_0_1_count, downcount_10_0_1_count[0], downcount_10_0_1_count[1], downcount_10_0_1_count[2], downcount_10_0_1_count[3], pedestrian_button_1_p6, downcount_10_0_1_count[2], downcount_10_0_1_count[1], downcount_10_0_1_count[0]
  _7_Segment_Display #(.active("false")) L_7_Segment_Display_2 (
    .g(HEX0[6]), .f(HEX0[5]), .a(HEX0[0]), .b(HEX0[1]), .e(HEX0[4]), .d(HEX0[3]), .c(HEX0[2]), .dp(HEX0[7]));
  // Bin2Hex_2 bin2hex_2_1: pin names not known; wires that end beside it: downcount_10_0_1_count[3], HEX1C, HEX0C

  // Other names for the same wires on the sheet: PA = ped_active

  // Notes on the sheet:
  //   Traffic Light A
  //   Counter Display
  //   Traffic Light B
  //   Counter_3sec
endmodule

module trial600 (
  input  in_1,
  input  ped_active,
  input  en
);

  wire and_1_out, and_2_out, and_3_out, clk, G, GB, GOFF, nState, or_1_out, or_2_out, or_3_out, or_4_out,
       or_5_out, or_6_out, or_7_out, or_8_out, pedestrian_button_1_p2, pedestrian_button_1_p3, R, RB, RON, Y,
       YB, YOFF;
  wire [3:0] downcount_10_0_1_count, DownCounter_v1_1_p3;
  wire [7:0] HEX0, HEX0C, HEX1, HEX1C;

  Button button_1 ();  // open: out
  and and_1 (and_1_out, ~DownCounter_v1_1_p3[0], ~DownCounter_v1_1_p3[1], ~DownCounter_v1_1_p3[2], ~DownCounter_v1_1_p3[3]);  // AND_Gate
  and and_2 (and_2_out, en, and_1_out);
  Clock u_clk (.out(clk));
  Multiplexer multiplexer_1 (.sel(in_1));  // open: in0, in1, out
  or or_1 (or_1_out, nState, pedestrian_button_1_p2);
  FULL_FSM full_fsm_1 (
    .ped_active(ped_active), .en(en), .next_state(and_2_out), .G_off(GOFF), .Y_off(YOFF), .R_on(RON),
    .GB(GB), .YB(YB), .RB(RB), .rst(nState), .GA(G), .YA(Y), .RA(R));
  // DownCounter_v1 DownCounter_v1_1: pin names not known; wires that end beside it: or_1_out, clk, DownCounter_v1_1_p3, DownCounter_v1_1_p3[3], DownCounter_v1_1_p3[2], DownCounter_v1_1_p3[1], DownCounter_v1_1_p3[0]
  // pedestrian_button pedestrian_button_1: pin names not known; wires that end beside it: DownCounter_v1_1_p3, pedestrian_button_1_p2
  // Bin2Hex_2 Bin2Hex_1: pin names not known; wires that end beside it: HEX1, HEX0
  or or_2 (or_2_out, R, RON);
  // RGBLED RGBLED_1: pin names not known; wires that end beside it: or_2_out
  or or_3 (or_3_out, Y, YOFF);
  // RGBLED RGBLED_2: pin names not known; wires that end beside it: or_3_out, or_3_out
  or or_4 (or_4_out, G, GOFF);
  // RGBLED RGBLED_3: pin names not known; wires that end beside it: or_4_out
  _7_Segment_Display #(.active("false")) u_7_segment_display_1 (
    .g(HEX1C[6]), .f(HEX1C[5]), .a(HEX1C[0]), .b(HEX1C[1]), .e(HEX1C[4]), .d(HEX1C[3]), .c(HEX1C[2]),
    .dp(HEX1C[7]));
  Clock clock_1 (.out(clk));
  or or_5 (or_5_out, ped_active, pedestrian_button_1_p3);
  _7_Segment_Display #(.active("false")) u_7_segment_display_2 (
    .g(HEX0C[6]), .f(HEX0C[5]), .a(HEX0C[0]), .b(HEX0C[1]), .e(HEX0C[4]), .d(HEX0C[3]), .c(HEX0C[2]),
    .dp(HEX0C[7]));
  or or_6 (or_6_out, RB, RON);
  // RGBLED rgbled_1: pin names not known; wires that end beside it: or_6_out
  or or_7 (or_7_out, YB, YOFF);
  // RGBLED rgbled_2: pin names not known; wires that end beside it: or_7_out, or_7_out
  or or_8 (or_8_out, GB, GOFF);
  // RGBLED rgbled_3: pin names not known; wires that end beside it: or_8_out
  _7_Segment_Display #(.active("false")) L_7_Segment_Display_1 (
    .g(HEX1[6]), .f(HEX1[5]), .a(HEX1[0]), .b(HEX1[1]), .e(HEX1[4]), .d(HEX1[3]), .c(HEX1[2]), .dp(HEX1[7]));
  and and_3 (and_3_out, ~downcount_10_0_1_count[0], ~downcount_10_0_1_count[1], ~downcount_10_0_1_count[2], ~downcount_10_0_1_count[3]);  // AND_Gate
  downcount_10_0 downcount_10_0_1 (.en(or_5_out), .clk(clk), .count(downcount_10_0_1_count));
  // pedestrian_button pedestrian_button_1: pin names not known; wires that end beside it: downcount_10_0_1_count, and_3_out, pedestrian_button_1_p3, downcount_10_0_1_count[2], downcount_10_0_1_count[1], downcount_10_0_1_count[0]
  _7_Segment_Display #(.active("false")) L_7_Segment_Display_2 (
    .g(HEX0[6]), .f(HEX0[5]), .a(HEX0[0]), .b(HEX0[1]), .e(HEX0[4]), .d(HEX0[3]), .c(HEX0[2]), .dp(HEX0[7]));
  // Bin2Hex_2 bin2hex_2_1: pin names not known; wires that end beside it: downcount_10_0_1_count[3], HEX1C, HEX0C

  // Other names for the same wires on the sheet: PA = ped_active

  // Notes on the sheet:
  //   Traffic Light A
  //   Counter Display
  //   Traffic Light B
  //   Counter_3sec
endmodule

module full_fsm3 (
  input  ped_active,
  input  en,
  input  next_state,
  output GB,
  output YB,
  output RB,
  output rst,
  output GA,
  output YA,
  output RA
);

  wire and_1_out, and_2_out, and_3_out, and_4_out, and_5_out, and_6_out, and_7_out, and_8_out, and_9_out,
       and_10_out, and_11_out, or_2_out, or_3_out;
  wire [1:0] register_2_q, register_3_q;
  wire [2:0] multiplexer_1_out, multiplexer_2_out, multiplexer_3_out, register_1_q;
  wire [2:1] undriven;
  wire [2:2] register_2_q_2, register_3_q_2;

  Multiplexer #(.width(3)) multiplexer_1 (
    .in0({undriven, en}), .in1(3'b100), .out(multiplexer_1_out), .sel(ped_active));
  Register #(.width(3)) register_1 (.D(multiplexer_1_out), .Q(register_1_q), .clk(next_state));  // open: en, clr
  Multiplexer #(.enable("true"), .select(3), .width(3)) multiplexer_2 (
    .in0(3'b000), .in1(3'b001), .in2(3'b010), .in3(3'b011), .in4(3'b001), .in5(3'b010), .in6(3'b011),
    .in7(3'b000), .out(multiplexer_2_out), .sel({en, register_2_q}));  // open: en
  // Probe on multiplexer_2_out
  Multiplexer #(.enable("true"), .select(3), .width(3)) multiplexer_3 (
    .in0(3'b000), .in1(3'b001), .in2(3'b010), .in3(3'b011), .in4(3'b001), .in5(3'b010), .in6(3'b011),
    .in7(3'b000), .out(multiplexer_3_out), .sel({en, register_3_q}));  // open: en
  Register #(.width(3)) register_2 (
    .D(multiplexer_2_out), .Q({register_2_q_2[2], register_2_q}), .clk(next_state));  // open: en, clr
  // Probe on {register_2_q_2[2], register_2_q}
  // Probe on multiplexer_3_out
  Register #(.width(3)) register_3 (
    .D(multiplexer_3_out), .Q({register_3_q_2[2], register_3_q}), .clk(next_state));  // open: en, clr
  and and_1 (and_1_out, register_1_q[0], register_1_q[1]);
  and and_2 (and_2_out, register_1_q[0], register_1_q[1]);
  and and_3 (and_3_out, ~register_1_q[0], ~register_1_q[1]);  // AND_Gate
  // Probe on {register_3_q_2[2], register_3_q}
  and and_4 (and_4_out, ~register_2_q[0], ~register_2_q[1]);  // AND_Gate
  and and_5 (and_5_out, register_2_q[0], ~register_2_q[1]);  // AND_Gate
  and and_6 (and_6_out, ~register_2_q[0], register_2_q[1]);  // AND_Gate
  and and_7 (and_7_out, register_2_q[0], register_2_q[1]);
  and and_8 (and_8_out, ~register_3_q[0], register_3_q[1]);  // AND_Gate
  and and_9 (and_9_out, register_3_q[0], register_3_q[1]);
  and and_10 (and_10_out, ~register_3_q[0], ~register_3_q[1]);  // AND_Gate
  and and_11 (and_11_out, register_3_q[0], ~register_3_q[1]);  // AND_Gate
  or or_1 (GB, and_1_out, and_4_out);
  or or_2 (or_2_out, and_6_out, and_7_out);
  or or_3 (or_3_out, and_10_out, and_11_out);
  or or_4 (YB, and_2_out, and_5_out);
  or or_5 (RB, or_2_out, and_3_out);
  or or_6 (GA, and_1_out, and_8_out);
  or or_7 (YA, and_9_out, and_2_out);
  or or_8 (RA, or_3_out, and_3_out);

  assign rst = next_state;

  // Notes on the sheet:
  //   Light B
  //   Light A
endmodule

module fullfsm4 (
  input  en,
  input  nxt_state,
  input  in_3,
  output RA,
  output GB,
  output reset,
  output RB,
  output YA,
  output YB,
  output GA
);

  wire and_1_out, and_2_out;
  wire [1:0] register_1_q;
  wire [2:0] multiplexer_2_out, undriven, undriven_2;
  wire [2:2] register_1_q_2;

  Multiplexer #(.width(3)) multiplexer_1 (.in1(undriven), .sel(in_3));  // open: in0, out
  Multiplexer #(.select(3), .width(3)) multiplexer_2 (
    .in0(3'b000), .in1(3'b001), .in2(3'b010), .in3(3'b011), .in4(undriven_2), .in6(3'b100),
    .out(multiplexer_2_out), .sel({en, register_1_q}));  // open: in5, in7
  // Probe on multiplexer_2_out
  Register #(.width(3)) register_1 (
    .D(multiplexer_2_out), .Q({register_1_q_2[2], register_1_q}), .clk(nxt_state));  // open: en, clr
  // Probe on {register_1_q_2[2], register_1_q}
  and and_1 (and_1_out, ~register_1_q[0], register_1_q[1]);  // AND_Gate
  and and_2 (and_2_out, ~register_1_q[0], register_1_q[1]);  // AND_Gate
  or or_1 (RA, and_1_out, and_2_out);

  assign reset = nxt_state;
endmodule

module CLOSER (
  input  ped_active,
  input  en
);

  wire and_1_out, and_2_out, and_3_out, and_4_out, and_5_out, and_6_out, clk, full_fsm_1_g_off,
       full_fsm_1_ga, full_fsm_1_gb, full_fsm_1_r_on, full_fsm_1_ra, full_fsm_1_rb, full_fsm_1_y_off,
       full_fsm_1_ya, full_fsm_1_yb, G, GB, nState, or_1_out, or_2_out, or_9_out, pedestrian_button_1_p2,
       pedestrian_button_1_p2_2, R, RB, Y, YB;
  wire [3:0] downcount_10_0_1_count, DownCounter_v1_1_p3;
  wire [7:0] HEX0, HEX0C, HEX1, HEX1C;

  and and_1 (and_1_out, and_6_out, ped_active);
  and and_2 (and_2_out, ~DownCounter_v1_1_p3[0], ~DownCounter_v1_1_p3[1], ~DownCounter_v1_1_p3[2], ~DownCounter_v1_1_p3[3]);  // AND_Gate
  Clock u_clk (.out(clk));
  and and_3 (and_3_out, nState, ~ped_active);  // AND_Gate
  or or_1 (or_1_out, and_1_out, and_4_out);
  and and_4 (and_4_out, en, and_2_out);
  or or_2 (or_2_out, and_3_out, pedestrian_button_1_p2);
  FULL_FSM full_fsm_1 (
    .ped_active(ped_active), .en(en), .next_state(or_1_out), .G_off(full_fsm_1_g_off),
    .Y_off(full_fsm_1_y_off), .R_on(full_fsm_1_r_on), .GB(full_fsm_1_gb), .YB(full_fsm_1_yb),
    .RB(full_fsm_1_rb), .rst(nState), .GA(full_fsm_1_ga), .YA(full_fsm_1_ya), .RA(full_fsm_1_ra));
  // DownCounter_v1 DownCounter_v1_1: pin names not known; wires that end beside it: or_2_out, clk, DownCounter_v1_1_p3, DownCounter_v1_1_p3[3], DownCounter_v1_1_p3[2], DownCounter_v1_1_p3[1], DownCounter_v1_1_p3[0]
  // pedestrian_button pedestrian_button_1: pin names not known; wires that end beside it: DownCounter_v1_1_p3, pedestrian_button_1_p2
  or or_3 (GB, full_fsm_1_g_off, full_fsm_1_gb);
  or or_4 (YB, full_fsm_1_y_off, full_fsm_1_yb);
  or or_5 (RB, full_fsm_1_r_on, full_fsm_1_rb);
  // Bin2Hex_2 Bin2Hex_1: pin names not known; wires that end beside it: HEX1, HEX0
  or or_6 (G, full_fsm_1_ga, full_fsm_1_g_off);
  or or_7 (Y, full_fsm_1_ya, full_fsm_1_y_off);
  or or_8 (R, full_fsm_1_ra, full_fsm_1_r_on);
  // RGBLED RGBLED_1: pin names not known; wires that end beside it: R
  // RGBLED RGBLED_2: pin names not known; wires that end beside it: Y, Y
  // RGBLED RGBLED_3: pin names not known; wires that end beside it: G
  _7_Segment_Display #(.active("false")) u_7_segment_display_1 (
    .g(HEX1C[6]), .f(HEX1C[5]), .a(HEX1C[0]), .b(HEX1C[1]), .e(HEX1C[4]), .d(HEX1C[3]), .c(HEX1C[2]),
    .dp(HEX1C[7]));
  Clock clock_1 (.out(clk));
  and and_5 (and_5_out, nState, ped_active);
  _7_Segment_Display #(.active("false")) u_7_segment_display_2 (
    .g(HEX0C[6]), .f(HEX0C[5]), .a(HEX0C[0]), .b(HEX0C[1]), .e(HEX0C[4]), .d(HEX0C[3]), .c(HEX0C[2]),
    .dp(HEX0C[7]));
  or or_9 (or_9_out, and_5_out, pedestrian_button_1_p2_2);
  // RGBLED rgbled_1: pin names not known; wires that end beside it: RB
  // RGBLED rgbled_2: pin names not known; wires that end beside it: YB, YB
  // RGBLED rgbled_3: pin names not known; wires that end beside it: GB
  and and_6 (and_6_out, downcount_10_0_1_count[0], downcount_10_0_1_count[1], downcount_10_0_1_count[2], downcount_10_0_1_count[3]);
  downcount_10_0 downcount_10_0_1 (.en(or_9_out), .clk(clk), .count(downcount_10_0_1_count));
  _7_Segment_Display #(.active("false")) L_7_Segment_Display_1 (
    .g(HEX1[6]), .f(HEX1[5]), .a(HEX1[0]), .b(HEX1[1]), .e(HEX1[4]), .d(HEX1[3]), .c(HEX1[2]), .dp(HEX1[7]));
  // pedestrian_button pedestrian_button_1: pin names not known; wires that end beside it: downcount_10_0_1_count, pedestrian_button_1_p2_2, downcount_10_0_1_count[2], downcount_10_0_1_count[1], downcount_10_0_1_count[0]
  _7_Segment_Display #(.active("false")) L_7_Segment_Display_2 (
    .g(HEX0[6]), .f(HEX0[5]), .a(HEX0[0]), .b(HEX0[1]), .e(HEX0[4]), .d(HEX0[3]), .c(HEX0[2]), .dp(HEX0[7]));
  // Bin2Hex_2 bin2hex_2_1: pin names not known; wires that end beside it: downcount_10_0_1_count[3], HEX1C, HEX0C

  // Other names for the same wires on the sheet: PA = ped_active

  // Notes on the sheet:
  //   Traffic Light A
  //   Counter Display
  //   Traffic Light B
  //   Counter_3sec
endmodule

module trial800 (
  input  ped_active,
  input  en,
  input  enable
);

  wire and_1_out, and_2_out, and_3_out, and_4_out, and_5_out, and_6_out, clk, full2fsm_1_g_off,
       full2fsm_1_ga, full2fsm_1_gb, full2fsm_1_r_on, full2fsm_1_ra, full2fsm_1_rb, full2fsm_1_y_off,
       full2fsm_1_ya, full2fsm_1_yb, G, GB, nState, or_1_out, or_8_out, PA_nstate, pedestrian_button_1_p2,
       pedestrian_button_1_p2_2, R, RB, Y, YB;
  wire [3:0] downcount_10_0_1_count, DownCounter_v1_1_p3;
  wire [7:0] HEX0, HEX0C, HEX1, HEX1C;

  and and_1 (and_1_out, ped_active, ~and_6_out);  // AND_Gate
  and and_2 (and_2_out, ~DownCounter_v1_1_p3[0], ~DownCounter_v1_1_p3[1], ~DownCounter_v1_1_p3[2], ~DownCounter_v1_1_p3[3]);  // AND_Gate
  and and_3 (and_3_out, ~ped_active, and_4_out);  // AND_Gate
  and and_4 (and_4_out, enable, and_2_out);
  Clock u_clk (.out(clk));
  or or_1 (or_1_out, nState, pedestrian_button_1_p2);
  full2fsm full2fsm_1 (
    .ped_active(ped_active), .nxt2(and_1_out), .enable(enable), .next_state(and_3_out),
    .G_off(full2fsm_1_g_off), .Y_off(full2fsm_1_y_off), .R_on(full2fsm_1_r_on), .rst2(PA_nstate),
    .GB(full2fsm_1_gb), .YB(full2fsm_1_yb), .RB(full2fsm_1_rb), .rst(nState), .GA(full2fsm_1_ga),
    .YA(full2fsm_1_ya), .RA(full2fsm_1_ra));
  // DownCounter_v1 DownCounter_v1_1: pin names not known; wires that end beside it: or_1_out, clk, DownCounter_v1_1_p3, DownCounter_v1_1_p3[3], DownCounter_v1_1_p3[2], DownCounter_v1_1_p3[1], DownCounter_v1_1_p3[0]
  // pedestrian_button pedestrian_button_1: pin names not known; wires that end beside it: DownCounter_v1_1_p3, pedestrian_button_1_p2
  or or_2 (GB, full2fsm_1_g_off, full2fsm_1_gb);
  or or_3 (YB, full2fsm_1_y_off, full2fsm_1_yb);
  or or_4 (RB, full2fsm_1_r_on, full2fsm_1_rb);
  or or_5 (G, full2fsm_1_g_off, full2fsm_1_ga);
  or or_6 (Y, full2fsm_1_ya, full2fsm_1_y_off);
  or or_7 (R, full2fsm_1_ra, full2fsm_1_r_on);
  // Bin2Hex_2 Bin2Hex_1: pin names not known; wires that end beside it: HEX1, HEX0
  // RGBLED RGBLED_1: pin names not known; wires that end beside it: R
  // RGBLED RGBLED_2: pin names not known; wires that end beside it: Y, Y
  // RGBLED RGBLED_3: pin names not known; wires that end beside it: G
  _7_Segment_Display #(.active("false")) u_7_segment_display_1 (
    .g(HEX1C[6]), .f(HEX1C[5]), .a(HEX1C[0]), .b(HEX1C[1]), .e(HEX1C[4]), .d(HEX1C[3]), .c(HEX1C[2]),
    .dp(HEX1C[7]));
  Clock clock_1 (.out(clk));
  and and_5 (and_5_out, ped_active, PA_nstate);
  or or_8 (or_8_out, and_5_out, pedestrian_button_1_p2_2);
  _7_Segment_Display #(.active("false")) u_7_segment_display_2 (
    .g(HEX0C[6]), .f(HEX0C[5]), .a(HEX0C[0]), .b(HEX0C[1]), .e(HEX0C[4]), .d(HEX0C[3]), .c(HEX0C[2]),
    .dp(HEX0C[7]));
  // RGBLED rgbled_1: pin names not known; wires that end beside it: RB
  // RGBLED rgbled_2: pin names not known; wires that end beside it: YB, YB
  // RGBLED rgbled_3: pin names not known; wires that end beside it: GB
  _7_Segment_Display #(.active("false")) L_7_Segment_Display_1 (
    .g(HEX1[6]), .f(HEX1[5]), .a(HEX1[0]), .b(HEX1[1]), .e(HEX1[4]), .d(HEX1[3]), .c(HEX1[2]), .dp(HEX1[7]));
  downcount_10_0 downcount_10_0_1 (.en(or_8_out), .clk(clk), .count(downcount_10_0_1_count));
  // pedestrian_button pedestrian_button_1: pin names not known; wires that end beside it: downcount_10_0_1_count, pedestrian_button_1_p2_2, downcount_10_0_1_count[2], downcount_10_0_1_count[1], downcount_10_0_1_count[0]
  _7_Segment_Display #(.active("false")) L_7_Segment_Display_2 (
    .g(HEX0[6]), .f(HEX0[5]), .a(HEX0[0]), .b(HEX0[1]), .e(HEX0[4]), .d(HEX0[3]), .c(HEX0[2]), .dp(HEX0[7]));
  and and_6 (and_6_out, downcount_10_0_1_count[0], downcount_10_0_1_count[1], downcount_10_0_1_count[2], downcount_10_0_1_count[3]);
  // Bin2Hex_2 bin2hex_2_1: pin names not known; wires that end beside it: downcount_10_0_1_count[3], HEX1C, HEX0C

  // Other names for the same wires on the sheet: PA = ped_active

  // Notes on the sheet:
  //   struggles to reset after ped_active goes back to 1
  //   Traffic Light A
  //   Counter Display
  //   Traffic Light B
  //   Counter_3sec
endmodule

module trial900 (
  input  ped_active,
  input  en
);

  wire and_1_out, and_2_out, and_3_out, and_4_out, and_5_out, and_6_out, clk, full_fsm_1_g_off,
       full_fsm_1_ga, full_fsm_1_gb, full_fsm_1_r_on, full_fsm_1_ra, full_fsm_1_rb, full_fsm_1_y_off,
       full_fsm_1_ya, full_fsm_1_yb, G, GB, nState, or_1_out, or_8_out, pedestrian_button_1_p2,
       pedestrian_button_1_p6, R, RB, Y, YB;
  wire [3:0] downcount_10_0_1_count, DownCounter_v1_1_p3;
  wire [7:0] HEX0, HEX0C, HEX1, HEX1C;

  and and_1 (and_1_out, ~DownCounter_v1_1_p3[0], ~DownCounter_v1_1_p3[1], ~DownCounter_v1_1_p3[2], ~DownCounter_v1_1_p3[3]);  // AND_Gate
  and and_2 (and_2_out, and_6_out, ped_active);
  and and_3 (and_3_out, en, and_1_out);
  Clock u_clk (.out(clk));
  and and_4 (and_4_out, ~and_2_out, and_3_out);  // AND_Gate
  or or_1 (or_1_out, nState, pedestrian_button_1_p2);
  FULL_FSM full_fsm_1 (
    .ped_active(ped_active), .en(en), .next_state(and_4_out), .G_off(full_fsm_1_g_off),
    .Y_off(full_fsm_1_y_off), .R_on(full_fsm_1_r_on), .GB(full_fsm_1_gb), .YB(full_fsm_1_yb),
    .RB(full_fsm_1_rb), .rst(nState), .GA(full_fsm_1_ga), .YA(full_fsm_1_ya), .RA(full_fsm_1_ra));
  // DownCounter_v1 DownCounter_v1_1: pin names not known; wires that end beside it: or_1_out, clk, DownCounter_v1_1_p3, DownCounter_v1_1_p3[3], DownCounter_v1_1_p3[2], DownCounter_v1_1_p3[1], DownCounter_v1_1_p3[0]
  // pedestrian_button pedestrian_button_1: pin names not known; wires that end beside it: DownCounter_v1_1_p3, pedestrian_button_1_p2
  or or_2 (GB, full_fsm_1_g_off, full_fsm_1_gb);
  or or_3 (YB, full_fsm_1_y_off, full_fsm_1_yb);
  or or_4 (RB, full_fsm_1_r_on, full_fsm_1_rb);
  or or_5 (G, full_fsm_1_ga, full_fsm_1_g_off);
  or or_6 (Y, full_fsm_1_ya, full_fsm_1_y_off);
  or or_7 (R, full_fsm_1_ra, full_fsm_1_r_on);
  // Bin2Hex_2 Bin2Hex_1: pin names not known; wires that end beside it: HEX1, HEX0
  // RGBLED RGBLED_1: pin names not known; wires that end beside it: R
  // RGBLED RGBLED_2: pin names not known; wires that end beside it: Y, Y
  // RGBLED RGBLED_3: pin names not known; wires that end beside it: G
  and and_5 (and_5_out, nState, ped_active);
  _7_Segment_Display #(.active("false")) u_7_segment_display_1 (
    .g(HEX1C[6]), .f(HEX1C[5]), .a(HEX1C[0]), .b(HEX1C[1]), .e(HEX1C[4]), .d(HEX1C[3]), .c(HEX1C[2]),
    .dp(HEX1C[7]));
  Clock clock_1 (.out(clk));
  _7_Segment_Display #(.active("false")) u_7_segment_display_2 (
    .g(HEX0C[6]), .f(HEX0C[5]), .a(HEX0C[0]), .b(HEX0C[1]), .e(HEX0C[4]), .d(HEX0C[3]), .c(HEX0C[2]),
    .dp(HEX0C[7]));
  or or_8 (or_8_out, and_5_out, pedestrian_button_1_p6);
  // RGBLED rgbled_1: pin names not known; wires that end beside it: RB
  // RGBLED rgbled_2: pin names not known; wires that end beside it: YB, YB
  // RGBLED rgbled_3: pin names not known; wires that end beside it: GB
  _7_Segment_Display #(.active("false")) L_7_Segment_Display_1 (
    .g(HEX1[6]), .f(HEX1[5]), .a(HEX1[0]), .b(HEX1[1]), .e(HEX1[4]), .d(HEX1[3]), .c(HEX1[2]), .dp(HEX1[7]));
  and and_6 (and_6_out, ~downcount_10_0_1_count[0], ~downcount_10_0_1_count[1], ~downcount_10_0_1_count[2], ~downcount_10_0_1_count[3]);  // AND_Gate
  downcount_10_0 downcount_10_0_1 (.en(or_8_out), .clk(clk), .count(downcount_10_0_1_count));
  // pedestrian_button pedestrian_button_1: pin names not known; wires that end beside it: downcount_10_0_1_count, downcount_10_0_1_count[0], downcount_10_0_1_count[1], downcount_10_0_1_count[2], downcount_10_0_1_count[3], pedestrian_button_1_p6, downcount_10_0_1_count[2], downcount_10_0_1_count[1], downcount_10_0_1_count[0]
  _7_Segment_Display #(.active("false")) L_7_Segment_Display_2 (
    .g(HEX0[6]), .f(HEX0[5]), .a(HEX0[0]), .b(HEX0[1]), .e(HEX0[4]), .d(HEX0[3]), .c(HEX0[2]), .dp(HEX0[7]));
  // Bin2Hex_2 bin2hex_2_1: pin names not known; wires that end beside it: downcount_10_0_1_count[3], HEX1C, HEX0C

  // Other names for the same wires on the sheet: PA = ped_active

  // Notes on the sheet:
  //   Traffic Light A
  //   Counter Display
  //   Traffic Light B
  //   Counter_3sec
endmodule

module CLOSER_2 (
  input  ped_active,
  input  en
);

  wire and_1_out, and_2_out, and_3_out, and_4_out, and_5_out, and_6_out, clk, full_fsm_1_g_off,
       full_fsm_1_ga, full_fsm_1_gb, full_fsm_1_r_on, full_fsm_1_ra, full_fsm_1_rb, full_fsm_1_y_off,
       full_fsm_1_ya, full_fsm_1_yb, G, GB, nState, or_1_out, or_2_out, or_9_out, pedestrian_button_1_p2,
       pedestrian_button_1_p6, R, RB, Y, YB;
  wire [3:0] downcount_10_0_1_count, DownCounter_v1_1_p3;
  wire [7:0] HEX0, HEX0C, HEX1, HEX1C;

  and and_1 (and_1_out, and_6_out, ped_active);
  and and_2 (and_2_out, ~DownCounter_v1_1_p3[0], ~DownCounter_v1_1_p3[1], ~DownCounter_v1_1_p3[2], ~DownCounter_v1_1_p3[3]);  // AND_Gate
  Clock u_clk (.out(clk));
  or or_1 (or_1_out, and_1_out, and_4_out);
  and and_3 (and_3_out, ~ped_active, en);  // AND_Gate
  and and_4 (and_4_out, en, and_2_out);
  or or_2 (or_2_out, nState, pedestrian_button_1_p2);
  FULL_FSM full_fsm_1 (
    .ped_active(ped_active), .en(and_3_out), .next_state(or_1_out), .G_off(full_fsm_1_g_off),
    .Y_off(full_fsm_1_y_off), .R_on(full_fsm_1_r_on), .GB(full_fsm_1_gb), .YB(full_fsm_1_yb),
    .RB(full_fsm_1_rb), .rst(nState), .GA(full_fsm_1_ga), .YA(full_fsm_1_ya), .RA(full_fsm_1_ra));
  // DownCounter_v1 DownCounter_v1_1: pin names not known; wires that end beside it: or_2_out, clk, DownCounter_v1_1_p3, DownCounter_v1_1_p3[3], DownCounter_v1_1_p3[2], DownCounter_v1_1_p3[1], DownCounter_v1_1_p3[0]
  // pedestrian_button pedestrian_button_1: pin names not known; wires that end beside it: DownCounter_v1_1_p3, pedestrian_button_1_p2
  or or_3 (GB, full_fsm_1_g_off, full_fsm_1_gb);
  or or_4 (YB, full_fsm_1_y_off, full_fsm_1_yb);
  or or_5 (RB, full_fsm_1_r_on, full_fsm_1_rb);
  // Bin2Hex_2 Bin2Hex_1: pin names not known; wires that end beside it: HEX1, HEX0
  or or_6 (G, full_fsm_1_ga, full_fsm_1_g_off);
  or or_7 (Y, full_fsm_1_ya, full_fsm_1_y_off);
  or or_8 (R, full_fsm_1_ra, full_fsm_1_r_on);
  // RGBLED RGBLED_1: pin names not known; wires that end beside it: R
  // RGBLED RGBLED_2: pin names not known; wires that end beside it: Y, Y
  // RGBLED RGBLED_3: pin names not known; wires that end beside it: G
  _7_Segment_Display #(.active("false")) u_7_segment_display_1 (
    .g(HEX1C[6]), .f(HEX1C[5]), .a(HEX1C[0]), .b(HEX1C[1]), .e(HEX1C[4]), .d(HEX1C[3]), .c(HEX1C[2]),
    .dp(HEX1C[7]));
  Clock clock_1 (.out(clk));
  and and_5 (and_5_out, nState, ped_active);
  _7_Segment_Display #(.active("false")) u_7_segment_display_2 (
    .g(HEX0C[6]), .f(HEX0C[5]), .a(HEX0C[0]), .b(HEX0C[1]), .e(HEX0C[4]), .d(HEX0C[3]), .c(HEX0C[2]),
    .dp(HEX0C[7]));
  or or_9 (or_9_out, and_5_out, pedestrian_button_1_p6);
  // RGBLED rgbled_1: pin names not known; wires that end beside it: RB
  // RGBLED rgbled_2: pin names not known; wires that end beside it: YB, YB
  // RGBLED rgbled_3: pin names not known; wires that end beside it: GB
  and and_6 (and_6_out, ~downcount_10_0_1_count[0], ~downcount_10_0_1_count[1], ~downcount_10_0_1_count[2], ~downcount_10_0_1_count[3]);  // AND_Gate
  downcount_10_0 downcount_10_0_1 (.en(or_9_out), .clk(clk), .count(downcount_10_0_1_count));
  _7_Segment_Display #(.active("false")) L_7_Segment_Display_1 (
    .g(HEX1[6]), .f(HEX1[5]), .a(HEX1[0]), .b(HEX1[1]), .e(HEX1[4]), .d(HEX1[3]), .c(HEX1[2]), .dp(HEX1[7]));
  // pedestrian_button pedestrian_button_1: pin names not known; wires that end beside it: downcount_10_0_1_count, downcount_10_0_1_count[0], downcount_10_0_1_count[1], downcount_10_0_1_count[2], downcount_10_0_1_count[3], pedestrian_button_1_p6, downcount_10_0_1_count[2], downcount_10_0_1_count[1], downcount_10_0_1_count[0]
  _7_Segment_Display #(.active("false")) L_7_Segment_Display_2 (
    .g(HEX0[6]), .f(HEX0[5]), .a(HEX0[0]), .b(HEX0[1]), .e(HEX0[4]), .d(HEX0[3]), .c(HEX0[2]), .dp(HEX0[7]));
  // Bin2Hex_2 bin2hex_2_1: pin names not known; wires that end beside it: downcount_10_0_1_count[3], HEX1C, HEX0C

  // Other names for the same wires on the sheet: PA = ped_active

  // Notes on the sheet:
  //   Traffic Light A
  //   Counter Display
  //   Traffic Light B
  //   Counter_3sec
endmodule

module trial_pause10 (
  input  ped_active,
  input  en
);

  wire and_1_out, and_2_out, and_3_out, and_4_out, and_5_out, and_6_out, and_7_out, clk, comparator_1_eq,
       comparator_1_gt, comparator_1_lt, full_fsm_1_g_off, full_fsm_1_ga, full_fsm_1_gb, full_fsm_1_r_on,
       full_fsm_1_ra, full_fsm_1_rb, full_fsm_1_y_off, full_fsm_1_ya, full_fsm_1_yb, G, GB, nState, or_1_out,
       or_2_out, or_9_out, or_10_out, pedestrian_button_1_p2, pedestrian_button_1_p6, R, RB, Y, YB;
  wire [3:0] downcount_10_0_1_count, DownCounter_v1_1_p3;
  wire [7:0] HEX0, HEX0C, HEX1, HEX1C;

  and and_1 (and_1_out, and_7_out, ped_active);
  and and_2 (and_2_out, ~DownCounter_v1_1_p3[0], ~DownCounter_v1_1_p3[1], ~DownCounter_v1_1_p3[2], ~DownCounter_v1_1_p3[3]);  // AND_Gate
  Clock u_clk (.out(clk));
  or or_1 (or_1_out, and_1_out, and_4_out);
  and and_3 (and_3_out, ~ped_active, en);  // AND_Gate
  and and_4 (and_4_out, en, and_2_out);
  or or_2 (or_2_out, nState, pedestrian_button_1_p2);
  FULL_FSM full_fsm_1 (
    .ped_active(ped_active), .en(and_3_out), .next_state(or_1_out), .G_off(full_fsm_1_g_off),
    .Y_off(full_fsm_1_y_off), .R_on(full_fsm_1_r_on), .GB(full_fsm_1_gb), .YB(full_fsm_1_yb),
    .RB(full_fsm_1_rb), .rst(nState), .GA(full_fsm_1_ga), .YA(full_fsm_1_ya), .RA(full_fsm_1_ra));
  // DownCounter_v1 DownCounter_v1_1: pin names not known; wires that end beside it: or_2_out, clk, DownCounter_v1_1_p3, DownCounter_v1_1_p3[3], DownCounter_v1_1_p3[2], DownCounter_v1_1_p3[1], DownCounter_v1_1_p3[0]
  // pedestrian_button pedestrian_button_1: pin names not known; wires that end beside it: DownCounter_v1_1_p3, pedestrian_button_1_p2
  or or_3 (GB, full_fsm_1_g_off, full_fsm_1_gb);
  or or_4 (YB, full_fsm_1_y_off, full_fsm_1_yb);
  or or_5 (RB, full_fsm_1_r_on, full_fsm_1_rb);
  or or_6 (G, full_fsm_1_ga, full_fsm_1_g_off);
  or or_7 (Y, full_fsm_1_ya, full_fsm_1_y_off);
  or or_8 (R, full_fsm_1_ra, full_fsm_1_r_on);
  // Bin2Hex_2 Bin2Hex_1: pin names not known; wires that end beside it: HEX1, HEX0
  // RGBLED RGBLED_1: pin names not known; wires that end beside it: R
  // RGBLED RGBLED_2: pin names not known; wires that end beside it: Y, Y
  // RGBLED RGBLED_3: pin names not known; wires that end beside it: G
  _7_Segment_Display #(.active("false")) u_7_segment_display_1 (
    .g(HEX1C[6]), .f(HEX1C[5]), .a(HEX1C[0]), .b(HEX1C[1]), .e(HEX1C[4]), .d(HEX1C[3]), .c(HEX1C[2]),
    .dp(HEX1C[7]));
  Clock clock_1 (.out(clk));
  and and_5 (and_5_out, nState, ped_active);
  _7_Segment_Display #(.active("false")) u_7_segment_display_2 (
    .g(HEX0C[6]), .f(HEX0C[5]), .a(HEX0C[0]), .b(HEX0C[1]), .e(HEX0C[4]), .d(HEX0C[3]), .c(HEX0C[2]),
    .dp(HEX0C[7]));
  or or_9 (or_9_out, and_5_out, pedestrian_button_1_p6);
  Comparator #(.width(4)) comparator_1 (
    .a(downcount_10_0_1_count), .b(4'b0000), .gt(comparator_1_gt), .eq(comparator_1_eq), .lt(comparator_1_lt));
  and and_6 (and_6_out, or_9_out, or_10_out);
  or or_10 (or_10_out, comparator_1_gt, comparator_1_lt);
  // RGBLED rgbled_1: pin names not known; wires that end beside it: RB
  // RGBLED rgbled_2: pin names not known; wires that end beside it: YB, YB
  // RGBLED rgbled_3: pin names not known; wires that end beside it: GB
  downcount_10_0 downcount_10_0_1 (.en(and_6_out), .clk(clk), .count(downcount_10_0_1_count));
  _7_Segment_Display #(.active("false")) L_7_Segment_Display_1 (
    .g(HEX1[6]), .f(HEX1[5]), .a(HEX1[0]), .b(HEX1[1]), .e(HEX1[4]), .d(HEX1[3]), .c(HEX1[2]), .dp(HEX1[7]));
  and and_7 (and_7_out, ~downcount_10_0_1_count[0], ~downcount_10_0_1_count[1], ~downcount_10_0_1_count[2], ~downcount_10_0_1_count[3]);  // AND_Gate
  // pedestrian_button pedestrian_button_1: pin names not known; wires that end beside it: downcount_10_0_1_count, downcount_10_0_1_count[0], downcount_10_0_1_count[1], downcount_10_0_1_count[2], downcount_10_0_1_count[3], pedestrian_button_1_p6, downcount_10_0_1_count[2], downcount_10_0_1_count[1], downcount_10_0_1_count[0]
  _7_Segment_Display #(.active("false")) L_7_Segment_Display_2 (
    .g(HEX0[6]), .f(HEX0[5]), .a(HEX0[0]), .b(HEX0[1]), .e(HEX0[4]), .d(HEX0[3]), .c(HEX0[2]), .dp(HEX0[7]));
  // Bin2Hex_2 bin2hex_2_1: pin names not known; wires that end beside it: downcount_10_0_1_count[3], HEX1C, HEX0C

  // Other names for the same wires on the sheet: PA = ped_active

  // Notes on the sheet:
  //   Traffic Light A
  //   Counter Display
  //   Traffic Light B
  //   Counter_3sec
endmodule

module global_fsm_LessOut (
  input  ped_active,
  input  en,
  input  next_state,
  output GB,
  output YB,
  output RB,
  output rst,
  output GA,
  output YA,
  output RA
);

  wire and_1_out, and_2_out, and_3_out, and_4_out, and_5_out, and_6_out, and_7_out, and_8_out, G_out,
       or_1_out, or_2_out, R_out, Y_out;
  wire [2:0] multiplexer_1_out, multiplexer_2_out, multiplexer_3_out, register_1_q, register_2_q,
       register_3_q;
  wire [2:1] undriven;

  Multiplexer #(.width(3)) multiplexer_1 (
    .in0({undriven, en}), .in1(3'b100), .out(multiplexer_1_out), .sel(ped_active));
  Register #(.width(3)) register_1 (.D(multiplexer_1_out), .Q(register_1_q), .clk(next_state));  // open: en, clr
  Multiplexer #(.enable("true"), .select(3), .width(3)) multiplexer_2 (
    .in0(3'b000), .in1(3'b001), .in2(3'b010), .in3(3'b011), .in4(3'b001), .in5(3'b010), .in6(3'b011),
    .in7(3'b000), .out(multiplexer_2_out), .sel({en, register_2_q[1:0]}));  // open: en
  // Probe on multiplexer_2_out
  Multiplexer #(.enable("true"), .select(3), .width(3)) multiplexer_3 (
    .in0(3'b000), .in1(3'b001), .in2(3'b010), .in3(3'b011), .in4(3'b001), .in5(3'b010), .in6(3'b011),
    .in7(3'b000), .out(multiplexer_3_out), .sel({en, register_3_q[1:0]}));  // open: en
  Register #(.width(3)) register_2 (.D(multiplexer_2_out), .Q(register_2_q), .clk(next_state));  // open: en, clr
  // Probe on register_2_q
  // Probe on multiplexer_3_out
  Register #(.width(3)) register_3 (.D(multiplexer_3_out), .Q(register_3_q), .clk(next_state));  // open: en, clr
  and G (G_out, register_1_q[0], register_1_q[1]);
  and Y (Y_out, register_1_q[0], register_1_q[1]);
  and R (R_out, ~register_1_q[0], ~register_1_q[1]);  // AND_Gate
  // Probe on register_3_q
  and and_1 (and_1_out, ~register_2_q[0], ~register_2_q[1]);  // AND_Gate
  and and_2 (and_2_out, register_2_q[0], ~register_2_q[1]);  // AND_Gate
  and and_3 (and_3_out, ~register_2_q[0], register_2_q[1]);  // AND_Gate
  and and_4 (and_4_out, register_2_q[0], register_2_q[1]);
  and and_5 (and_5_out, ~register_3_q[0], register_3_q[1]);  // AND_Gate
  and and_6 (and_6_out, register_3_q[0], register_3_q[1]);
  and and_7 (and_7_out, ~register_3_q[0], ~register_3_q[1]);  // AND_Gate
  and and_8 (and_8_out, register_3_q[0], ~register_3_q[1]);  // AND_Gate
  or or_1 (or_1_out, and_3_out, and_4_out);
  or or_2 (or_2_out, and_7_out, and_8_out);
  or or_3 (GB, G_out, and_1_out);
  or or_4 (YB, Y_out, and_2_out);
  or or_5 (RB, R_out, or_1_out);
  or or_6 (GA, G_out, and_5_out);
  or or_7 (YA, Y_out, and_6_out);
  or or_8 (RA, R_out, or_2_out);

  assign rst = next_state;

  // Notes on the sheet:
  //   Light B
  //   Light A
endmodule

module trial1200 (
  input  ped_active,
  input  en
);

  wire and_1_out, and_2_out, and_3_out, and_4_out, and_5_out, and_6_out, clk, G, GB, nState, or_1_out,
       or_2_out, or_3_out, pedestrian_button_1_p2, pedestrian_button_1_p2_2, R, RB, Y, YB;
  wire [3:0] downcount_10_0_1_count, DownCounter_v1_1_p3;
  wire [7:0] HEX0, HEX0C, HEX1, HEX1C;

  and and_1 (and_1_out, and_6_out, ped_active);
  and and_2 (and_2_out, ~DownCounter_v1_1_p3[0], ~DownCounter_v1_1_p3[1], ~DownCounter_v1_1_p3[2], ~DownCounter_v1_1_p3[3]);  // AND_Gate
  or or_1 (or_1_out, and_1_out, and_4_out);
  and and_3 (and_3_out, ~ped_active, en);  // AND_Gate
  and and_4 (and_4_out, en, and_2_out);
  Clock u_clk (.out(clk));
  or or_2 (or_2_out, nState, pedestrian_button_1_p2);
  global_fsm_LessOut global_fsm_lessout_1 (
    .ped_active(ped_active), .en(and_3_out), .next_state(or_1_out), .GB(GB), .YB(YB), .RB(RB), .rst(nState),
    .GA(G), .YA(Y), .RA(R));
  // DownCounter_v1 DownCounter_v1_1: pin names not known; wires that end beside it: or_2_out, clk, DownCounter_v1_1_p3, DownCounter_v1_1_p3[3], DownCounter_v1_1_p3[2], DownCounter_v1_1_p3[1], DownCounter_v1_1_p3[0]
  // pedestrian_button pedestrian_button_1: pin names not known; wires that end beside it: DownCounter_v1_1_p3, pedestrian_button_1_p2
  // Bin2Hex_2 Bin2Hex_1: pin names not known; wires that end beside it: HEX1, HEX0
  // RGBLED RGBLED_1: pin names not known; wires that end beside it: R
  // RGBLED RGBLED_2: pin names not known; wires that end beside it: Y, Y
  // RGBLED RGBLED_3: pin names not known; wires that end beside it: G
  _7_Segment_Display #(.active("false")) u_7_segment_display_1 (
    .g(HEX1C[6]), .f(HEX1C[5]), .a(HEX1C[0]), .b(HEX1C[1]), .e(HEX1C[4]), .d(HEX1C[3]), .c(HEX1C[2]),
    .dp(HEX1C[7]));
  Clock clock_1 (.out(clk));
  and and_5 (and_5_out, nState, ped_active);
  or or_3 (or_3_out, and_5_out, pedestrian_button_1_p2_2);
  _7_Segment_Display #(.active("false")) u_7_segment_display_2 (
    .g(HEX0C[6]), .f(HEX0C[5]), .a(HEX0C[0]), .b(HEX0C[1]), .e(HEX0C[4]), .d(HEX0C[3]), .c(HEX0C[2]),
    .dp(HEX0C[7]));
  // RGBLED rgbled_1: pin names not known; wires that end beside it: RB
  // RGBLED rgbled_2: pin names not known; wires that end beside it: YB, YB
  // RGBLED rgbled_3: pin names not known; wires that end beside it: GB
  _7_Segment_Display #(.active("false")) L_7_Segment_Display_1 (
    .g(HEX1[6]), .f(HEX1[5]), .a(HEX1[0]), .b(HEX1[1]), .e(HEX1[4]), .d(HEX1[3]), .c(HEX1[2]), .dp(HEX1[7]));
  and and_6 (and_6_out, ~downcount_10_0_1_count[0], ~downcount_10_0_1_count[1], ~downcount_10_0_1_count[2], ~downcount_10_0_1_count[3]);  // AND_Gate
  downcount_10_0 downcount_10_0_1 (.en(or_3_out), .clk(clk), .count(downcount_10_0_1_count));
  // pedestrian_button pedestrian_button_1: pin names not known; wires that end beside it: downcount_10_0_1_count, pedestrian_button_1_p2_2, downcount_10_0_1_count[2], downcount_10_0_1_count[1], downcount_10_0_1_count[0]
  _7_Segment_Display #(.active("false")) L_7_Segment_Display_2 (
    .g(HEX0[6]), .f(HEX0[5]), .a(HEX0[0]), .b(HEX0[1]), .e(HEX0[4]), .d(HEX0[3]), .c(HEX0[2]), .dp(HEX0[7]));
  // Bin2Hex_2 bin2hex_2_1: pin names not known; wires that end beside it: downcount_10_0_1_count[3], HEX1C, HEX0C

  // Other names for the same wires on the sheet: PA = ped_active

  // Notes on the sheet:
  //   Traffic Light A
  //   Counter Display
  //   Traffic Light B
  //   Counter_3sec
endmodule

module Global_FSM_trial3 (
  input  en,
  input  nxt_state,
  output GA,
  output YA,
  output RA,
  output GB,
  output YB,
  output RB,
  output rst
);

  wire and_3_out, and_4_out, and_5_out, not_1_out, not_2_out, not_3_out;
  wire [2:0] register_1_q;
  wire [3:0] multiplexer_1_out;
  wire [3:3] register_1_q_2;

  Multiplexer #(.select(4), .width(4)) multiplexer_1 (
    .in0(4'b0000), .in1(4'b0001), .in2(4'b0010), .in3(4'b0011), .in4(4'b0100), .in5(4'b0101), .in6(4'b0001),
    .in7(4'b0010), .in8(4'b0011), .in9(4'b0100), .in10(4'b0101), .in11(4'b0000), .out(multiplexer_1_out),
    .sel({en, register_1_q}));  // open: in12, in13, in14, in15
  Register #(.width(4)) register_1 (
    .D(multiplexer_1_out), .Q({register_1_q_2[3], register_1_q}), .clk(nxt_state));  // open: en, clr
  not not_1 (not_1_out, register_1_q[0]);
  not not_2 (not_2_out, register_1_q[1]);
  not not_3 (not_3_out, register_1_q[2]);
  and and_1 (GA, not_1_out, register_1_q[1], register_1_q[2]);
  and and_2 (YA, register_1_q[0], not_2_out, not_3_out);
  and and_3 (and_3_out, not_1_out, not_2_out);
  and and_4 (and_4_out, register_1_q[1], not_3_out);
  and and_5 (and_5_out, register_1_q[0], register_1_q[2]);
  and and_6 (GB, not_1_out, not_2_out, not_3_out);
  and and_7 (YB, not_1_out, not_2_out, register_1_q[2]);
  or or_1 (RB, register_1_q[1], register_1_q[0]);
  or or_2 (RA, and_3_out, and_4_out, and_5_out);

  assign rst = nxt_state;
endmodule

module logic_lights (
  input  S0,
  input  S1,
  input  S2,
  output GA,
  output YA,
  output RA,
  output GB,
  output YB,
  output RB
);

  wire and_3_out, and_4_out, and_5_out, not_1_out, not_2_out, not_3_out;

  not not_1 (not_1_out, S0);
  not not_2 (not_2_out, S1);
  not not_3 (not_3_out, S2);
  and and_1 (GA, not_1_out, S1, S2);
  and and_2 (YA, S0, not_2_out, not_3_out);
  and and_3 (and_3_out, not_1_out, not_2_out);
  and and_4 (and_4_out, S1, not_3_out);
  and and_5 (and_5_out, S0, S2);
  and and_6 (GB, not_1_out, not_2_out, not_3_out);
  and and_7 (YB, not_1_out, not_2_out, S2);
  or or_1 (RB, S1, S0);
  or or_2 (RA, and_3_out, and_4_out, and_5_out);
endmodule

module new_FSMLights (
  input  en
);

  wire and_1_out, and_2_out, clk, G, GB, nState, or_1_out, pedestrian_button_1_p2, R, RB, Y, YB;
  wire [3:0] DownCounter_v1_1_p3;
  wire [7:0] HEX0, HEX1;

  and and_1 (and_1_out, ~DownCounter_v1_1_p3[0], ~DownCounter_v1_1_p3[1], ~DownCounter_v1_1_p3[2], ~DownCounter_v1_1_p3[3]);  // AND_Gate
  and and_2 (and_2_out, en, and_1_out);
  Clock u_clk (.out(clk));
  or or_1 (or_1_out, nState, pedestrian_button_1_p2);
  Global_FSM_trial3 global_fsm_trial3_1 (
    .en(en), .nxt_state(and_2_out), .GA(G), .YA(Y), .RA(R), .GB(GB), .YB(YB), .RB(RB), .rst(nState));
  // DownCounter_v1 DownCounter_v1_1: pin names not known; wires that end beside it: or_1_out, clk, DownCounter_v1_1_p3, DownCounter_v1_1_p3[3], DownCounter_v1_1_p3[2], DownCounter_v1_1_p3[1], DownCounter_v1_1_p3[0]
  // pedestrian_button pedestrian_button_1: pin names not known; wires that end beside it: DownCounter_v1_1_p3, pedestrian_button_1_p2
  // Bin2Hex_2 Bin2Hex_1: pin names not known; wires that end beside it: HEX1, HEX0
  // RGBLED RGBLED_1: pin names not known; wires that end beside it: R
  // RGBLED RGBLED_2: pin names not known; wires that end beside it: Y, Y
  // RGBLED RGBLED_3: pin names not known; wires that end beside it: G
  // RGBLED rgbled_1: pin names not known; wires that end beside it: RB
  // RGBLED rgbled_2: pin names not known; wires that end beside it: YB, YB
  // RGBLED rgbled_3: pin names not known; wires that end beside it: GB
  _7_Segment_Display #(.active("false")) L_7_Segment_Display_1 (
    .g(HEX1[6]), .f(HEX1[5]), .a(HEX1[0]), .b(HEX1[1]), .e(HEX1[4]), .d(HEX1[3]), .c(HEX1[2]), .dp(HEX1[7]));
  _7_Segment_Display #(.active("false")) L_7_Segment_Display_2 (
    .g(HEX0[6]), .f(HEX0[5]), .a(HEX0[0]), .b(HEX0[1]), .e(HEX0[4]), .d(HEX0[3]), .c(HEX0[2]), .dp(HEX0[7]));

  // Notes on the sheet:
  //   Traffic Light A
  //   Traffic Light B
  //   Counter_3sec
endmodule
