// Logisim project Lab_5_Dreiling.circ as structural Verilog
module HA (
  input  X,
  input  Y,
  output S,
  output C
);

  wire and_1_out, and_2_out, not_1_out, not_2_out;

  not not_1 (not_1_out, X);
  not not_2 (not_2_out, Y);
  and and_1 (and_1_out, not_1_out, Y);
  and and_2 (and_2_out, X, not_2_out);
  and and_3 (C, X, Y);
  or or_1 (S, and_1_out, and_2_out);
endmodule

module RippleCarry (
  input  [3:0] x,
  input  Cin,
  input  [3:0] y,
  output [3:0] z,
  output cout
);

  wire FA2_cout, FA3_cout, fa_1_cout;

  FA fa_1 (.cin(Cin), .x(x[0]), .y(y[0]), .cout(fa_1_cout), .z(z[0]));
  FA FA2 (.cin(fa_1_cout), .x(x[1]), .y(y[1]), .cout(FA2_cout), .z(z[1]));
  FA FA3 (.cin(FA2_cout), .x(x[2]), .y(y[2]), .cout(FA3_cout), .z(z[2]));
  FA FA4 (.cin(FA3_cout), .x(x[3]), .y(y[3]), .cout(cout), .z(z[3]));
endmodule

module test_circuit (
  input  in_1,
  input  in_2,
  input  in_3,
  input  [3:0] in_4,
  input  in_5,
  input  [3:0] in_6,
  output out_7,
  output out_8,
  output out_9,
  output out_10,
  output [3:0] out_11,
  output out_12
);

  HA ha_1 (.X(in_1), .Y(in_2), .S(out_7), .C(out_8));
  FA fa_1 (.cin(in_3), .x(in_1), .y(in_2), .cout(out_9), .z(out_10));
  RippleCarry ripplecarry_1 (.x(in_4), .Cin(in_5), .y(in_6), .z(out_11), .cout(out_12));
endmodule

module FA (
  input  cin,
  input  x,
  input  y,
  output cout,
  output z
);

  wire and_1_out, and_2_out, and_3_out, and_4_out, and_5_out, and_6_out, and_7_out, not_1_out, not_2_out,
       not_3_out;

  not not_1 (not_1_out, cin);
  not not_2 (not_2_out, x);
  not not_3 (not_3_out, y);
  and and_1 (and_1_out, x, y);
  and and_2 (and_2_out, cin, y);
  and and_3 (and_3_out, cin, x);
  and and_4 (and_4_out, not_1_out, not_2_out, y);
  and and_5 (and_5_out, not_1_out, x, not_3_out);
  and and_6 (and_6_out, cin, not_2_out, not_3_out);
  and and_7 (and_7_out, cin, x, y);
  or or_1 (cout, and_1_out, and_2_out, and_3_out);
  or or_2 (z, and_4_out, and_5_out, and_6_out, and_7_out);
endmodule

module subtracter (
  input  s,
  input  [3:0] b,
  input  [3:0] a,
  output [3:0] sum,
  output out_5
);

  wire [3:0] xor_4_out;

  xor xor_1 (xor_4_out[3], s, b[3]);
  xor xor_2 (xor_4_out[2], s, b[2]);
  xor xor_3 (xor_4_out[1], s, b[1]);
  RippleCarry ripplecarry_1 (.x(a), .Cin(s), .y(xor_4_out), .z(sum), .cout(out_5));
  xor xor_4 (xor_4_out[0], s, b[0]);
endmodule

module RippleCarry_Ground (
  input  [3:0] x,
  input  [3:0] y,
  output [3:0] z,
  output cout
);

  wire FA2_cout, FA3_cout, fa_1_cout;

  FA fa_1 (.cin(1'b0), .x(x[0]), .y(y[0]), .cout(fa_1_cout), .z(z[0]));
  FA FA2 (.cin(fa_1_cout), .x(x[1]), .y(y[1]), .cout(FA2_cout), .z(z[1]));
  FA FA3 (.cin(FA2_cout), .x(x[2]), .y(y[2]), .cout(FA3_cout), .z(z[2]));
  FA FA4 (.cin(FA3_cout), .x(x[3]), .y(y[3]), .cout(cout), .z(z[3]));
endmodule
