// Logisim project lab8_ENCE2101_Dreiling.circ as structural Verilog: 5 circuits, main circuit main
module main (
  input  Input_1,
  input  Input_2,
  input  Input_3,
  output Output_1,
  output Output_2,
  output Output_3
);


  assign Output_1 = Input_1;
  assign Output_2 = Input_2;
  assign Output_3 = Input_3;
endmodule

module cyle_8_1sec (
  output G,
  output Y,
  output R
);

  wire clock_1_out;

  Counter #(.max('h7), .width(3)) counter_1 (.Q({R, Y, G}), .clk(clock_1_out));  // open: load, D, count, carry, up, clr
  Clock clock_1 (.out(clock_1_out));
endmodule

module three_pattern_switch (
  input  switch_1,
  input  Switch_2,
  output G,
  output Y,
  output R
);

  wire and_1_out, and_2_out, and_3_out, and_4_out, clock_1_out;
  wire [2:0] counter_1_q;

  Clock clock_1 (.out(clock_1_out));
  Counter #(.max('h7), .width(3)) counter_1 (
    .Q(counter_1_q), .clk(clock_1_out));  // open: load, D, count, carry, up, clr
  and and_1 (and_1_out, switch_1, Switch_2, counter_1_q[0]);
  and and_2 (and_2_out, counter_1_q[0], ~Switch_2, counter_1_q[0]);  // AND_Gate
  and and_3 (and_3_out, switch_1, Switch_2, counter_1_q[1]);
  and and_4 (and_4_out, ~switch_1, Switch_2, counter_1_q[1]);  // AND_Gate
  and and_5 (R, switch_1, Switch_2, counter_1_q[2]);
  or or_1 (Y, and_3_out, and_4_out);
  or or_2 (G, and_1_out, and_2_out);
endmodule

module blinkRed (
);

  wire undriven;
  wire [2:0] counter_1_q;

  Counter #(.max('h7), .width(3)) counter_1 (.Q(counter_1_q), .clk(undriven));  // open: load, D, count, carry, up, clr
endmodule

module possiblesolution (
  input  [1:0] switch,
  output G,
  output Y,
  output R
);

  wire clock_1_out;
  wire [2:0] counter_1_q;

  Counter #(.max('h7), .width(3)) counter_1 (
    .Q(counter_1_q), .clk(clock_1_out));  // open: load, D, count, carry, up, clr
  Clock clock_1 (.out(clock_1_out));
  Multiplexer #(.select(2), .width(3)) multiplexer_1 (
    .in0(counter_1_q), .in1({counter_1_q[2], 2'b00}), .in2({2'b00, counter_1_q[0]}), .out({R, Y, G}),
    .sel(switch));  // open: in3
endmodule
